// Logisim project DataMemory.circ as structural Verilog: 5 circuits, main circuit main
module main (
  input  [3:0] icode,
  input  [63:0] ValE,
  input  [63:0] ValA,
  input  [63:0] ValP,
  input  Clk,
  output [63:0] ValM
);

  wire clock_1_out, comparator_1_eq, decoder_1_out0, decoder_1_out1, decoder_1_out2, decoder_1_out3,
       decoder_1_out4, decoder_1_out5, decoder_1_out6, decoder_1_out7, memread_1_read, memwrite_1_write;
  wire [7:0] adder_1_out, demultiplexer_1_out0, demultiplexer_1_out1, demultiplexer_1_out2,
       demultiplexer_1_out3, demultiplexer_1_out4, demultiplexer_1_out5, demultiplexer_1_out6,
       demultiplexer_1_out7, multiplexer_1_out, multiplexer_2_out, ram_1_dout, register_1_q;
  wire [11:0] adder_2_out, bit_extender_1_out;
  wire [63:0] memaddr_1_addr, memdata_1_data;

  Clock clock_1 (.out(clock_1_out));
  Register register_1 (.D(multiplexer_1_out), .clk(clock_1_out), .Q(register_1_q));  // open: en, clr
  Adder adder_1 (.a(register_1_q), .b(8'h1), .out(adder_1_out));  // open: cin, cout
  Comparator #(.mode("unsigned")) comparator_1 (.a(adder_1_out), .b(8'h8), .eq(comparator_1_eq));  // open: gt, lt
  MemAddr memaddr_1 (.ValE(ValE), .ValA(ValA), .icode(icode), .addr(memaddr_1_addr));
  MemWrite memwrite_1 (.icode(icode), .write(memwrite_1_write));
  MemRead memread_1 (.icode(icode), .read(memread_1_read));
  MemData memdata_1 (.ValP(ValP), .ValA(ValA), .icode(icode), .data(memdata_1_data));
  Multiplexer #(.width(8)) multiplexer_1 (
    .in0(adder_1_out), .in1({8{1'b0}}), .out(multiplexer_1_out), .sel(comparator_1_eq));
  assign bit_extender_1_out = {{4{1'b0}}, multiplexer_1_out};  // Bit_Extender bit_extender_1
  Adder #(.width(12)) adder_2 (.a(memaddr_1_addr[11:0]), .b(bit_extender_1_out), .out(adder_2_out));  // open: cin, cout
  Multiplexer #(.select(3), .width(8)) multiplexer_2 (
    .in0(memdata_1_data[7:0]), .in1(memdata_1_data[15:8]), .in2(memdata_1_data[23:16]),
    .in3(memdata_1_data[31:24]), .in4(memdata_1_data[39:32]), .in5(memdata_1_data[47:40]),
    .in6(memdata_1_data[55:48]), .in7(memdata_1_data[63:56]), .out(multiplexer_2_out),
    .sel(bit_extender_1_out[2:0]));
  RAM #(.addrWidth(12)) ram_1 (
    .addr(adder_2_out), .we(memwrite_1_write), .oe(memread_1_read), .clk(clock_1_out),
    .din(multiplexer_2_out), .dout(ram_1_dout));
  Demultiplexer #(.select(3), .width(8)) demultiplexer_1 (
    .out0(demultiplexer_1_out0), .out1(demultiplexer_1_out1), .out2(demultiplexer_1_out2),
    .out3(demultiplexer_1_out3), .out4(demultiplexer_1_out4), .out5(demultiplexer_1_out5),
    .out6(demultiplexer_1_out6), .out7(demultiplexer_1_out7), .in(ram_1_dout), .sel(bit_extender_1_out[2:0]));
  Decoder #(.enable("false"), .select(3)) decoder_1 (
    .out0(decoder_1_out0), .out1(decoder_1_out1), .out2(decoder_1_out2), .out3(decoder_1_out3),
    .out4(decoder_1_out4), .out5(decoder_1_out5), .out6(decoder_1_out6), .out7(decoder_1_out7),
    .sel(bit_extender_1_out[2:0]));
  Register register_2 (.D(demultiplexer_1_out0), .en(decoder_1_out0), .clk(clock_1_out), .Q(ValM[63:56]));  // open: clr
  Register register_3 (.D(demultiplexer_1_out1), .en(decoder_1_out1), .clk(clock_1_out), .Q(ValM[7:0]));  // open: clr
  Register register_4 (.D(demultiplexer_1_out2), .en(decoder_1_out2), .clk(clock_1_out), .Q(ValM[15:8]));  // open: clr
  Register register_5 (.D(demultiplexer_1_out3), .en(decoder_1_out3), .clk(clock_1_out), .Q(ValM[23:16]));  // open: clr
  Register register_6 (.D(demultiplexer_1_out4), .en(decoder_1_out4), .clk(clock_1_out), .Q(ValM[31:24]));  // open: clr
  Register register_7 (.D(demultiplexer_1_out5), .en(decoder_1_out5), .clk(clock_1_out), .Q(ValM[39:32]));  // open: clr
  Register register_8 (.D(demultiplexer_1_out6), .en(decoder_1_out6), .clk(clock_1_out), .Q(ValM[47:40]));  // open: clr
  Register register_9 (.D(demultiplexer_1_out7), .en(decoder_1_out7), .clk(clock_1_out), .Q(ValM[55:48]));  // open: clr
endmodule

module MemRead (
  input  [3:0] icode,
  output read
);

  wire comparator_1_eq, comparator_2_eq, comparator_3_eq;

  Comparator #(.mode("unsigned"), .width(4)) comparator_1 (
    .a(icode), .b(4'b0101), .eq(comparator_1_eq));  // open: gt, lt
  Comparator #(.mode("unsigned"), .width(4)) comparator_2 (
    .a(icode), .b(4'b1001), .eq(comparator_2_eq));  // open: gt, lt
  Comparator #(.mode("unsigned"), .width(4)) comparator_3 (
    .a(icode), .b(4'b1011), .eq(comparator_3_eq));  // open: gt, lt
  or or_1 (read, comparator_1_eq, comparator_2_eq, comparator_3_eq);
endmodule

module MemWrite (
  input  [3:0] icode,
  output write
);

  wire comparator_1_eq, comparator_2_eq, comparator_3_eq, comparator_4_eq;

  Comparator #(.mode("unsigned"), .width(4)) comparator_1 (
    .a(icode), .b(4'b0010), .eq(comparator_1_eq));  // open: gt, lt
  Comparator #(.mode("unsigned"), .width(4)) comparator_2 (
    .a(icode), .b(4'b0100), .eq(comparator_2_eq));  // open: gt, lt
  Comparator #(.mode("unsigned"), .width(4)) comparator_3 (
    .a(icode), .b(4'b1000), .eq(comparator_3_eq));  // open: gt, lt
  Comparator #(.mode("unsigned"), .width(4)) comparator_4 (
    .a(icode), .b(4'b1010), .eq(comparator_4_eq));  // open: gt, lt
  or or_1 (write, comparator_1_eq, comparator_2_eq, comparator_3_eq, comparator_4_eq);
endmodule

module MemAddr (
  input  [63:0] ValE,
  input  [63:0] ValA,
  input  [3:0] icode,
  output [63:0] addr
);

  wire comparator_1_eq, comparator_2_eq, comparator_3_eq, comparator_4_eq, comparator_5_eq, comparator_6_eq,
       comparator_7_eq;
  wire [1:0] or_1_out;

  Comparator #(.mode("unsigned"), .width(4)) comparator_1 (
    .a(icode), .b(4'b0010), .eq(comparator_1_eq));  // open: gt, lt
  Comparator #(.mode("unsigned"), .width(4)) comparator_2 (
    .a(icode), .b(4'b0100), .eq(comparator_2_eq));  // open: gt, lt
  Comparator #(.mode("unsigned"), .width(4)) comparator_3 (
    .a(icode), .b(4'b0101), .eq(comparator_3_eq));  // open: gt, lt
  Comparator #(.mode("unsigned"), .width(4)) comparator_4 (
    .a(icode), .b(4'b1000), .eq(comparator_4_eq));  // open: gt, lt
  Comparator #(.mode("unsigned"), .width(4)) comparator_5 (
    .a(icode), .b(4'b1010), .eq(comparator_5_eq));  // open: gt, lt
  Comparator #(.mode("unsigned"), .width(4)) comparator_6 (
    .a(icode), .b(4'b1001), .eq(comparator_6_eq));  // open: gt, lt
  Comparator #(.mode("unsigned"), .width(4)) comparator_7 (
    .a(icode), .b(4'b1011), .eq(comparator_7_eq));  // open: gt, lt
  or or_1 (or_1_out[0], comparator_1_eq, comparator_2_eq, comparator_3_eq, comparator_4_eq, comparator_5_eq);
  or or_2 (or_1_out[1], comparator_6_eq, comparator_7_eq);
  Multiplexer #(.select(2), .width(64)) multiplexer_1 (
    .in1(ValE), .in2(ValA), .out(addr), .sel(or_1_out));  // open: in0, in3
endmodule

module MemData (
  input  [63:0] ValP,
  input  [63:0] ValA,
  input  [3:0] icode,
  output [63:0] data
);

  wire comparator_1_eq, comparator_2_eq, comparator_3_eq;
  wire [1:0] or_1_out;

  Comparator #(.mode("unsigned"), .width(4)) comparator_1 (
    .a(icode), .b(4'b0010), .eq(comparator_1_eq));  // open: gt, lt
  Comparator #(.mode("unsigned"), .width(4)) comparator_2 (
    .a(icode), .b(4'b0100), .eq(comparator_2_eq));  // open: gt, lt
  Comparator #(.mode("unsigned"), .width(4)) comparator_3 (
    .a(icode), .b(4'b1010), .eq(comparator_3_eq));  // open: gt, lt
  Comparator #(.mode("unsigned"), .width(4)) comparator_4 (.a(icode), .b(4'b1000), .eq(or_1_out[1]));  // open: gt, lt
  or or_1 (or_1_out[0], comparator_1_eq, comparator_2_eq, comparator_3_eq);
  Multiplexer #(.select(2), .width(64)) multiplexer_1 (
    .in1(ValP), .in2(ValA), .out(data), .sel(or_1_out));  // open: in0, in3
endmodule
