// Logisim project EXECUTE.circ as structural Verilog: 8 circuits, main circuit main
module main (
  input  [7:0] cycles,
  input  clk,
  input  [3:0] ifun,
  input  setcc,
  input  z,
  input  s,
  input  o,
  output cond
);
endmodule

module EXECUTE (
  input  [7:0] cyc_cnt,
  input  clk,
  input  [3:0] icode,
  input  [3:0] ifun,
  input  [63:0] valC,
  input  [63:0] valA,
  input  [63:0] valB,
  output condition,
  output [63:0] valE
);

  wire alu_1_o, alu_1_s, alu_1_z, setcc_1_set_cc;
  wire [1:0] alu_fun_1_alufun;
  wire [63:0] alu_a_1_op1, alu_b_1_op2;

  setCC setcc_1 (.icode(icode), .set_cc(setcc_1_set_cc));
  ALU_A alu_a_1 (.icode(icode), .val_c(valC), .val_a(valA), .op1(alu_a_1_op1));
  ALU_B alu_b_1 (.icode(icode), .valB(valB), .op2(alu_b_1_op2));
  ALU_FUN alu_fun_1 (.ifun(ifun), .icode(icode), .alufun(alu_fun_1_alufun));
  ALU alu_1 (
    .op1(alu_a_1_op1), .op2(alu_b_1_op2), .funcType(alu_fun_1_alufun), .z(alu_1_z), .o(alu_1_o), .s(alu_1_s),
    .valE(valE));
  Cond cond_1 (
    .cycles(cyc_cnt), .clk(clk), .ifun(ifun), .setcc(setcc_1_set_cc), .z(alu_1_z), .s(alu_1_s), .o(alu_1_o),
    .cond(condition));
endmodule

module ALU (
  input  [63:0] op1,
  input  [63:0] op2,
  input  [1:0] funcType,
  output z,
  output o,
  output s,
  output [63:0] valE
);

  wire [63:0] adder_1_out, adder_2_out, and_1_out, xor_1_out;

  Adder #(.width(64)) adder_1 (.a(op1), .b(op1), .out(adder_1_out), .cout(o));  // open: cin
  Adder #(.width(64)) adder_2 (.a(op2), .b(op1), .out(adder_2_out), .cout(s));  // open: cin
  assign and_1_out = op1 & op2;  // AND_Gate and_1, 64 bits wide
  assign xor_1_out = op1 ^ op2;  // XOR_Gate xor_1, 64 bits wide
  Multiplexer #(.select(2), .width(64)) multiplexer_1 (
    .in0(adder_1_out), .in1(adder_2_out), .in2(and_1_out), .in3(xor_1_out), .out(valE), .sel(funcType));
  Comparator #(.width(64)) comparator_1 (.a(64'h1), .b(valE), .eq(z));  // open: gt, lt
endmodule

module ALU_B (
  input  [3:0] icode,
  input  [63:0] valB,
  output [63:0] op2
);

  wire comparator_1_eq, comparator_2_eq, comparator_3_eq, comparator_4_eq, comparator_5_eq, or_1_out,
       or_2_out;

  Comparator #(.width(4)) comparator_1 (.a(icode), .b(4'b0110), .eq(comparator_1_eq));  // open: gt, lt
  Comparator #(.width(4)) comparator_2 (.a(icode), .b(4'b0100), .eq(comparator_2_eq));  // open: gt, lt
  Comparator #(.width(4)) comparator_3 (.a(icode), .b(4'b0101), .eq(comparator_3_eq));  // open: gt, lt
  Comparator #(.width(4)) comparator_4 (.a(icode), .b(4'b0011), .eq(comparator_4_eq));  // open: gt, lt
  Comparator #(.width(4)) comparator_5 (.a(icode), .b(4'b0010), .eq(comparator_5_eq));  // open: gt, lt
  or or_1 (or_1_out, comparator_1_eq, comparator_2_eq, comparator_3_eq);
  or or_2 (or_2_out, comparator_4_eq, comparator_5_eq);
  assign op2 = or_1_out ? valB : 64'bz;  // Controlled_Buffer controlled_buffer_1
  assign op2 = or_2_out ? {64{1'b0}} : 64'bz;  // Controlled_Buffer controlled_buffer_2

  // Notes on the sheet:
  //   opq
  //   rmmovq
  //   mrmovq
  //   irmovq
  //   rrmovq
endmodule

module ALU_A (
  input  [3:0] icode,
  input  [63:0] val_c,
  input  [63:0] val_a,
  output [63:0] op1
);

  wire comparator_1_eq, comparator_2_eq, comparator_3_eq, comparator_4_eq, comparator_5_eq, or_1_out,
       or_2_out;

  Comparator #(.width(4)) comparator_1 (.a(icode), .b(4'b0010), .eq(comparator_1_eq));  // open: gt, lt
  Comparator #(.width(4)) comparator_2 (.a(icode), .b(4'b0110), .eq(comparator_2_eq));  // open: gt, lt
  Comparator #(.width(4)) comparator_3 (.a(icode), .b(4'b0011), .eq(comparator_3_eq));  // open: gt, lt
  Comparator #(.width(4)) comparator_4 (.a(icode), .b(4'b0100), .eq(comparator_4_eq));  // open: gt, lt
  Comparator #(.width(4)) comparator_5 (.a(icode), .b(4'b0101), .eq(comparator_5_eq));  // open: gt, lt
  or or_1 (or_1_out, comparator_3_eq, comparator_4_eq, comparator_5_eq);
  or or_2 (or_2_out, comparator_1_eq, comparator_2_eq);
  assign op1 = or_1_out ? val_c : 64'bz;  // Controlled_Buffer controlled_buffer_1
  assign op1 = or_2_out ? val_a : 64'bz;  // Controlled_Buffer controlled_buffer_2

  // Notes on the sheet:
  //   rrmovq
  //   opq
  //   rmmovq
  //   mrmovq
  //   irmovq
endmodule

module ALU_FUN (
  input  [3:0] ifun,
  input  [3:0] icode,
  output [1:0] alufun
);

  wire comparator_1_eq, comparator_2_eq, or_1_out;
  wire [3:2] multiplexer_1_out;

  Comparator #(.width(4)) comparator_1 (.a(4'b0111), .b(icode), .eq(comparator_1_eq));  // open: gt, lt
  Comparator #(.width(4)) comparator_2 (.a(icode), .b(4'b0110), .eq(comparator_2_eq));  // open: gt, lt
  or or_1 (or_1_out, comparator_1_eq, comparator_2_eq);
  Multiplexer #(.width(4)) multiplexer_1 (.in0(4'b0000), .in1(ifun), .out({multiplexer_1_out, alufun}), .sel(or_1_out));
endmodule

module setCC (
  input  [3:0] icode,
  output set_cc
);

  wire comparator_1_eq;

  Comparator #(.width(4)) comparator_1 (.a(icode), .b(4'b0110), .eq(comparator_1_eq));  // open: gt, lt
  Multiplexer multiplexer_1 (.in0(1'b0), .in1(1'b1), .out(set_cc), .sel(comparator_1_eq));
endmodule

module Cond (
  input  [7:0] cycles,
  input  clk,
  input  [3:0] ifun,
  input  setcc,
  input  z,
  input  s,
  input  o,
  output cond
);

  wire and_1_out, comparator_1_eq, multiplexer_1_out, nand_1_out, not_1_out, not_2_out, not_3_out, not_4_out,
       or_1_out, xor_1_out;

  not not_1 (not_1_out, z);
  not not_2 (not_2_out, s);
  not not_3 (not_3_out, o);
  Comparator comparator_1 (.a(cycles), .b(8'hb), .eq(comparator_1_eq));  // open: gt, lt
  and and_1 (and_1_out, comparator_1_eq, clk, setcc);
  xor xor_1 (xor_1_out, s, o);
  or or_1 (or_1_out, xor_1_out, z);
  not not_4 (not_4_out, xor_1_out);
  nand nand_1 (nand_1_out, xor_1_out, z);
  Multiplexer #(.select(4)) multiplexer_1 (
    .in0(1'b1), .in1(or_1_out), .in2(xor_1_out), .in3(z), .in4(not_1_out), .in5(not_4_out), .in6(nand_1_out),
    .out(multiplexer_1_out), .sel(ifun));  // open: in7, in8, in9, in10, in11, in12, in13, in14, in15
  D_Flip_Flop d_ff_1 (.D(multiplexer_1_out), .clk(and_1_out), .Q(cond));  // open: Qn, preset, reset
endmodule
