// Logisim project exec.circ as structural Verilog: 3 circuits, main circuit main
module main (
  input  [7:0] cycles,
  input  clk,
  input  [3:0] ifun,
  input  setcc,
  input  z,
  input  s,
  input  o,
  output cond
);

  wire and_1_out, comparator_1_eq, multiplexer_1_out, nand_1_out, not_1_out, not_2_out, not_3_out, not_4_out,
       or_1_out, xor_1_out;

  not not_1 (not_1_out, z);
  not not_2 (not_2_out, s);
  not not_3 (not_3_out, o);
  Comparator comparator_1 (.a(cycles), .b(8'hb), .eq(comparator_1_eq));  // open: gt, lt
  and and_1 (and_1_out, comparator_1_eq, clk, setcc);
  xor xor_1 (xor_1_out, s, o);
  or or_1 (or_1_out, xor_1_out, z);
  not not_4 (not_4_out, xor_1_out);
  nand nand_1 (nand_1_out, xor_1_out, z);
  Multiplexer #(.select(4)) multiplexer_1 (
    .in0(1'b1), .in1(or_1_out), .in2(xor_1_out), .in3(z), .in4(not_1_out), .in5(not_4_out), .in6(nand_1_out),
    .out(multiplexer_1_out), .sel(ifun));  // open: in7, in8, in9, in10, in11, in12, in13, in14, in15
  D_Flip_Flop d_ff_1 (.D(multiplexer_1_out), .clk(and_1_out), .Q(cond));  // open: Qn, preset, reset
endmodule

module alu_a (
  input  [3:0] icode,
  input  [63:0] val_c,
  input  [63:0] val_a,
  output [63:0] op1
);

  wire comparator_1_eq, comparator_2_eq, comparator_3_eq, comparator_4_eq, comparator_5_eq, or_1_out,
       or_2_out;

  Comparator #(.width(4)) comparator_1 (.a(icode), .b(4'b0010), .eq(comparator_1_eq));  // open: gt, lt
  Comparator #(.width(4)) comparator_2 (.a(icode), .b(4'b0110), .eq(comparator_2_eq));  // open: gt, lt
  Comparator #(.width(4)) comparator_3 (.a(icode), .b(4'b0011), .eq(comparator_3_eq));  // open: gt, lt
  Comparator #(.width(4)) comparator_4 (.a(icode), .b(4'b0100), .eq(comparator_4_eq));  // open: gt, lt
  Comparator #(.width(4)) comparator_5 (.a(icode), .b(4'b0101), .eq(comparator_5_eq));  // open: gt, lt
  or or_1 (or_1_out, comparator_3_eq, comparator_4_eq, comparator_5_eq);
  or or_2 (or_2_out, comparator_1_eq, comparator_2_eq);
  assign op1 = or_1_out ? val_c : 64'bz;  // Controlled_Buffer controlled_buffer_1
  assign op1 = or_2_out ? val_a : 64'bz;  // Controlled_Buffer controlled_buffer_2

  // Notes on the sheet:
  //   rrmovq
  //   opq
  //   rmmovq
  //   mrmovq
  //   irmovq
endmodule

module alu_b (
  input  [3:0] icode,
  input  [63:0] valB,
  output [63:0] op2
);

  wire comparator_1_eq, comparator_2_eq, comparator_3_eq, comparator_4_eq, comparator_5_eq, or_1_out,
       or_2_out;

  Comparator #(.width(4)) comparator_1 (.a(icode), .b(4'b0110), .eq(comparator_1_eq));  // open: gt, lt
  Comparator #(.width(4)) comparator_2 (.a(icode), .b(4'b0100), .eq(comparator_2_eq));  // open: gt, lt
  Comparator #(.width(4)) comparator_3 (.a(icode), .b(4'b0101), .eq(comparator_3_eq));  // open: gt, lt
  Comparator #(.width(4)) comparator_4 (.a(icode), .b(4'b0011), .eq(comparator_4_eq));  // open: gt, lt
  Comparator #(.width(4)) comparator_5 (.a(icode), .b(4'b0010), .eq(comparator_5_eq));  // open: gt, lt
  or or_1 (or_1_out, comparator_1_eq, comparator_2_eq, comparator_3_eq);
  or or_2 (or_2_out, comparator_4_eq, comparator_5_eq);
  assign op2 = or_1_out ? valB : 64'bz;  // Controlled_Buffer controlled_buffer_1
  assign op2 = or_2_out ? {64{1'b0}} : 64'bz;  // Controlled_Buffer controlled_buffer_2

  // Notes on the sheet:
  //   opq
  //   rmmovq
  //   mrmovq
  //   irmovq
  //   rrmovq
endmodule
