// Logisim project fetch.circ as structural Verilog: 7 circuits, main circuit main
module main (
  input  [11:0] PC,
  input  [7:0] cycle,
  input  clk,
  output [3:0] ifun,
  output [3:0] icode,
  output [3:0] rA,
  output [3:0] rB,
  output [63:0] ValC,
  output [11:0] ValP
);

  wire need_regids_1_needs_register, need_valc_1_needs_valc;
  wire [7:0] fetch_instruction_memory_1_s1, fetch_instruction_memory_1_s2, fetch_instruction_memory_1_s3,
       fetch_instruction_memory_1_s4, fetch_instruction_memory_1_s5, fetch_instruction_memory_1_s6,
       fetch_instruction_memory_1_s7, fetch_instruction_memory_1_s8, fetch_instruction_memory_1_s9;

  fetch_instruction_memory fetch_instruction_memory_1 (
    .PC(PC), .cycle(cycle), .clk(clk), .s0({icode, ifun}), .s1(fetch_instruction_memory_1_s1),
    .s2(fetch_instruction_memory_1_s2), .s3(fetch_instruction_memory_1_s3),
    .s4(fetch_instruction_memory_1_s4), .s5(fetch_instruction_memory_1_s5),
    .s6(fetch_instruction_memory_1_s6), .s7(fetch_instruction_memory_1_s7),
    .s8(fetch_instruction_memory_1_s8), .s9(fetch_instruction_memory_1_s9));
  fetch_allign fetch_allign_1 (
    .Byte1(fetch_instruction_memory_1_s1), .Byte2(fetch_instruction_memory_1_s2),
    .Byte3(fetch_instruction_memory_1_s3), .Byte4(fetch_instruction_memory_1_s4),
    .Byte5(fetch_instruction_memory_1_s5), .Byte6(fetch_instruction_memory_1_s6),
    .Byte7(fetch_instruction_memory_1_s7), .Byte8(fetch_instruction_memory_1_s8),
    .Byte9(fetch_instruction_memory_1_s9), .needs_register(need_regids_1_needs_register), .R_A(rA), .R_B(rB),
    .out_13(ValC));
  need_regids need_regids_1 (.icode(icode), .needs_register(need_regids_1_needs_register));
  need_valC need_valc_1 (.icode(icode), .needs_ValC(need_valc_1_needs_valc));
  pc_increment pc_increment_1 (
    .need_reg(need_regids_1_needs_register), .imm_value(need_valc_1_needs_valc), .PC(PC), .cycle(cycle),
    .ValP(ValP));

  // Notes on the sheet:
  //   splits the first byte
endmodule

module fetch_instruction_memory (
  input  [11:0] PC,
  input  [7:0] cycle,
  input  clk,
  output [7:0] s0,
  output [7:0] s1,
  output [7:0] s2,
  output [7:0] s3,
  output [7:0] s4,
  output [7:0] s5,
  output [7:0] s6,
  output [7:0] s7,
  output [7:0] s8,
  output [7:0] s9
);

  wire comparator_1_gt, decoder_1_out0, decoder_1_out1, decoder_1_out2, decoder_1_out3, decoder_1_out4,
       decoder_1_out5, decoder_1_out6, decoder_1_out7, decoder_1_out8, decoder_1_out9;
  wire [7:0] demultiplexer_1_out0, demultiplexer_1_out1, demultiplexer_1_out2, demultiplexer_1_out3,
       demultiplexer_1_out4, demultiplexer_1_out5, demultiplexer_1_out6, demultiplexer_1_out7,
       demultiplexer_1_out8, demultiplexer_1_out9, multiplexer_1_out, rom_1_data;
  wire [11:0] adder_1_out, bit_extender_1_out;

  Clock clock_1 ();  // open: out
  Multiplexer #(.width(8)) multiplexer_1 (.in0(8'h9), .in1(cycle), .out(multiplexer_1_out), .sel(comparator_1_gt));
  Comparator comparator_1 (.a(8'ha), .b(cycle), .gt(comparator_1_gt));  // open: eq, lt
  assign bit_extender_1_out = {{4{multiplexer_1_out[7]}}, multiplexer_1_out};  // Bit_Extender bit_extender_1
  Adder #(.width(12)) adder_1 (.a(PC), .b(bit_extender_1_out), .out(adder_1_out));  // open: cin, cout
  ROM #(.addrWidth(12)) rom_1 (.addr(adder_1_out), .data(rom_1_data));
  Demultiplexer #(.select(4), .width(8)) demultiplexer_1 (
    .out0(demultiplexer_1_out0), .out1(demultiplexer_1_out1), .out2(demultiplexer_1_out2),
    .out3(demultiplexer_1_out3), .out4(demultiplexer_1_out4), .out5(demultiplexer_1_out5),
    .out6(demultiplexer_1_out6), .out7(demultiplexer_1_out7), .out8(demultiplexer_1_out8),
    .out9(demultiplexer_1_out9), .in(rom_1_data), .sel(multiplexer_1_out[3:0]));  // open: out10, out11, out12, out13, out14, out15
  Decoder #(.enable("false"), .select(4)) decoder_1 (
    .out0(decoder_1_out0), .out1(decoder_1_out1), .out2(decoder_1_out2), .out3(decoder_1_out3),
    .out4(decoder_1_out4), .out5(decoder_1_out5), .out6(decoder_1_out6), .out7(decoder_1_out7),
    .out8(decoder_1_out8), .out9(decoder_1_out9), .sel(multiplexer_1_out[3:0]));  // open: out10, out11, out12, out13, out14, out15
  Register register_1 (.D(demultiplexer_1_out0), .en(decoder_1_out0), .clk(clk), .Q(s0));  // open: clr
  Register register_2 (.D(demultiplexer_1_out1), .en(decoder_1_out1), .clk(clk), .Q(s1));  // open: clr
  Register register_3 (.D(demultiplexer_1_out2), .en(decoder_1_out2), .clk(clk), .Q(s2));  // open: clr
  Register register_4 (.D(demultiplexer_1_out3), .en(decoder_1_out3), .clk(clk), .Q(s3));  // open: clr
  Register register_5 (.D(demultiplexer_1_out4), .en(decoder_1_out4), .clk(clk), .Q(s4));  // open: clr
  Register register_6 (.D(demultiplexer_1_out5), .en(decoder_1_out5), .clk(clk), .Q(s5));  // open: clr
  Register register_7 (.D(demultiplexer_1_out6), .en(decoder_1_out6), .clk(clk), .Q(s6));  // open: clr
  Register register_8 (.D(demultiplexer_1_out7), .en(decoder_1_out7), .clk(clk), .Q(s7));  // open: clr
  Register register_9 (.D(demultiplexer_1_out8), .en(decoder_1_out8), .clk(clk), .Q(s8));  // open: clr
  Register register_10 (.D(demultiplexer_1_out9), .en(decoder_1_out9), .clk(clk), .Q(s9));  // open: clr

  // Notes on the sheet:
  //   contents of rom_1 (hex, n*v repeats v):
  //   30 f0 a 7*0 30 f1 a 7*0 30 f2 2 7*0 30 f3 1
endmodule

module need_regids (
  input  [3:0] icode,
  output needs_register
);

  wire comparator_1_eq, comparator_2_eq, comparator_3_eq, comparator_4_eq, comparator_5_eq, comparator_6_eq,
       comparator_7_eq;

  Comparator #(.width(4)) comparator_1 (.a(icode), .b(4'b0010), .eq(comparator_1_eq));  // open: gt, lt
  Comparator #(.width(4)) comparator_2 (.a(icode), .b(4'b0011), .eq(comparator_2_eq));  // open: gt, lt
  Comparator #(.width(4)) comparator_3 (.a(icode), .b(4'b0100), .eq(comparator_3_eq));  // open: gt, lt
  Comparator #(.width(4)) comparator_4 (.a(icode), .b(4'b0101), .eq(comparator_4_eq));  // open: gt, lt
  Comparator #(.width(4)) comparator_5 (.a(icode), .b(4'b0110), .eq(comparator_5_eq));  // open: gt, lt
  Comparator #(.width(4)) comparator_6 (.a(icode), .b(4'b1010), .eq(comparator_6_eq));  // open: gt, lt
  Comparator #(.width(4)) comparator_7 (.a(icode), .b(4'b1011), .eq(comparator_7_eq));  // open: gt, lt
  or or_1 (needs_register, comparator_1_eq, comparator_2_eq, comparator_3_eq, comparator_4_eq, comparator_5_eq, comparator_6_eq, comparator_7_eq);

  // Notes on the sheet:
  //   rrmovq
  //   irmovq
  //   rmmovq
  //   mrmovq
  //   opl
  //   pushq
  //   popq
endmodule

module need_valC (
  input  [3:0] icode,
  output needs_ValC
);

  wire comparator_1_eq, comparator_2_eq, comparator_3_eq, comparator_4_eq, comparator_5_eq;

  Comparator #(.width(4)) comparator_1 (.a(icode), .b(4'b0011), .eq(comparator_1_eq));  // open: gt, lt
  Comparator #(.width(4)) comparator_2 (.a(icode), .b(4'b0100), .eq(comparator_2_eq));  // open: gt, lt
  Comparator #(.width(4)) comparator_3 (.a(icode), .b(4'b0101), .eq(comparator_3_eq));  // open: gt, lt
  Comparator #(.width(4)) comparator_4 (.a(icode), .b(4'b0111), .eq(comparator_4_eq));  // open: gt, lt
  Comparator #(.width(4)) comparator_5 (.a(icode), .b(4'b1000), .eq(comparator_5_eq));  // open: gt, lt
  or or_1 (needs_ValC, comparator_1_eq, comparator_2_eq, comparator_3_eq, comparator_4_eq, comparator_5_eq);

  // Notes on the sheet:
  //   irmovq
  //   rmmovq
  //   mrmovq
  //   jxx
  //   call
endmodule

module pc_increment (
  input  need_reg,
  input  imm_value,
  input  [11:0] PC,
  input  [7:0] cycle,
  output [11:0] ValP
);

  wire adder_1_cout, adder_2_cout;
  wire [11:0] adder_1_out, adder_2_out, multiplexer_1_out, multiplexer_2_out;

  Multiplexer #(.width(12)) multiplexer_1 (.in0({12{1'b0}}), .in1(12'h1), .out(multiplexer_1_out), .sel(need_reg));
  Multiplexer #(.width(12)) multiplexer_2 (.in0({12{1'b0}}), .in1(12'h8), .out(multiplexer_2_out), .sel(imm_value));
  Adder #(.width(12)) adder_1 (.a(multiplexer_2_out), .b(PC), .out(adder_1_out), .cout(adder_1_cout));  // open: cin
  Adder #(.width(12)) adder_2 (
    .a(multiplexer_1_out), .b(adder_1_out), .out(adder_2_out), .cin(adder_1_cout), .cout(adder_2_cout));
  Adder #(.width(12)) adder_3 (.a(adder_2_out), .b({4'b0000, cycle}), .out(ValP), .cin(adder_2_cout));  // open: cout
endmodule

module fetch_allign (
  input  [7:0] Byte1,
  input  [7:0] Byte2,
  input  [7:0] Byte3,
  input  [7:0] Byte4,
  input  [7:0] Byte5,
  input  [7:0] Byte6,
  input  [7:0] Byte7,
  input  [7:0] Byte8,
  input  [7:0] Byte9,
  input  needs_register,
  output [3:0] R_A,
  output [3:0] R_B,
  output [63:0] out_13
);

  Multiplexer #(.width(8)) multiplexer_1 (.in1(Byte1), .out({R_B, R_A}), .sel(needs_register));  // open: in0
  Multiplexer #(.width(64)) multiplexer_2 (
    .in0({Byte1, Byte2, Byte3, Byte4, Byte5, Byte6, Byte7, Byte8}),
    .in1({Byte2, Byte3, Byte4, Byte5, Byte6, Byte7, Byte8, Byte9}), .out(out_13), .sel(needs_register));
endmodule

module fetch_main (
  output [11:0] number_instructions
);

  wire clock_1_out, comparator_1_eq, comparator_2_gt, comparator_3_lt;
  wire [7:0] adder_1_out, multiplexer_2_out, register_1_q;
  wire [11:0] adder_2_out, main_1_valp, multiplexer_1_out;

  Clock clock_1 (.out(clock_1_out));
  Register register_1 (.D(multiplexer_2_out), .Q(register_1_q));  // open: en, clk, clr
  Comparator comparator_1 (.a(8'h13), .b(adder_1_out), .eq(comparator_1_eq));  // open: gt, lt
  Register #(.width(12)) register_2 (
    .D(adder_2_out), .en(comparator_1_eq), .clk(clock_1_out), .Q(number_instructions));  // open: clr
  Adder adder_1 (.a(register_1_q), .b(8'h1), .out(adder_1_out));  // open: cin, cout
  Multiplexer #(.width(12)) multiplexer_1 (
    .in0({12{1'b0}}), .in1(main_1_valp), .out(multiplexer_1_out), .sel(comparator_3_lt));
  Multiplexer #(.width(8)) multiplexer_2 (
    .in0({8{1'b0}}), .in1(adder_1_out), .out(multiplexer_2_out), .sel(comparator_2_gt));
  Comparator comparator_2 (.a(8'h14), .b(adder_1_out), .gt(comparator_2_gt));  // open: eq, lt
  Adder #(.width(12)) adder_2 (.a(12'h1), .b(number_instructions), .out(adder_2_out));  // open: cin, cout
  Comparator #(.width(12)) comparator_3 (
    .a({12{1'b0}}), .b(number_instructions), .lt(comparator_3_lt));  // open: gt, eq
  main main_1 (
    .PC(multiplexer_1_out), .cycle(register_1_q), .clk(clock_1_out), .ValP(main_1_valp));  // open: ifun, icode, rA, rB, ValC
endmodule
