// Logisim project F_TTL_Gates.circ as structural Verilog: 1 circuit, main circuit main
module main (
  input  in_1,
  input  in_2,
  input  in_3,
  input  in_4,
  input  in_5,
  input  in_6,
  output out_7,
  output out_8
);

  wire and_1_out, and_2_out, and_3_out, and_4_out, n7408_1_pin3, n7408_1_pin6, n7408_1_pin8, n7408_1_pin11,
       n7408_2_pin11, n7432_1_pin3, n7432_1_pin5;

  _7408 #(.ShowInternalStructure("true")) u_7408_1 (
    .pin1(in_5), .pin2(in_4), .pin3(n7408_1_pin3), .pin4(in_5), .pin5(in_6), .pin6(n7408_1_pin6),
    .pin13(in_4), .pin12(in_5), .pin11(n7408_1_pin11), .pin10(n7408_1_pin11), .pin9(in_6), .pin8(n7408_1_pin8));
  _7408 #(.ShowInternalStructure("true")) u_7408_2 (
    .pin13(in_4), .pin12(in_6), .pin11(n7408_2_pin11));  // open: pin1, pin2, pin3, pin4, pin5, pin6, pin10, pin9, pin8
  and and_1 (and_1_out, in_1, in_2, in_3);
  and and_2 (and_2_out, in_1, in_2);
  and and_3 (and_3_out, in_2, in_3);
  and and_4 (and_4_out, in_1, in_3);
  _7432 #(.ShowInternalStructure("true")) u_7432_1 (
    .pin1(n7408_1_pin6), .pin2(n7408_2_pin11), .pin3(n7432_1_pin3), .pin4(n7432_1_pin3), .pin5(n7432_1_pin5),
    .pin6(out_8), .pin13(n7408_1_pin3), .pin12(n7408_1_pin8), .pin11(n7432_1_pin5));  // open: pin10, pin9, pin8
  or or_1 (out_7, and_1_out, and_2_out, and_3_out, and_4_out);

  // Notes on the sheet:
  //   abc
  //   ab
  //   bc
  //   ca
endmodule
