// Logisim project G_TTL_Gates.circ as structural Verilog: 1 circuit, main circuit main
module main (
  input  a,
  input  b,
  input  c,
  input  a_2,
  input  b_2,
  input  c_2,
  output out_7,
  output out_8
);

  wire and_1_out, and_2_out, and_3_out, n7400_1_pin3, n7402_1_pin13, n7408_1_pin3, n7408_1_pin8,
       n7408_1_pin11, n7432_1_pin11, not_1_out, not_2_out, not_3_out;

  not not_1 (not_1_out, c);
  not not_2 (not_2_out, a);
  not not_3 (not_3_out, b);
  _7402 #(.ShowInternalStructure("true")) u_7402_1 (
    .pin13(n7402_1_pin13), .pin12(a_2), .pin11(c_2));  // open: pin1, pin2, pin3, pin4, pin5, pin6, pin10, pin9, pin8
  and and_1 (and_1_out, not_2_out, not_1_out);
  and and_2 (and_2_out, a, not_3_out, c);
  and and_3 (and_3_out, b, c);
  _7400 #(.ShowInternalStructure("true")) u_7400_1 (
    .pin1(b_2), .pin2(b_2), .pin3(n7400_1_pin3));  // open: pin4, pin5, pin6, pin13, pin12, pin11, pin10, pin9, pin8
  or or_1 (out_7, and_1_out, and_2_out, and_3_out);
  _7408 #(.ShowInternalStructure("true")) u_7408_1 (
    .pin1(b_2), .pin2(c_2), .pin3(n7408_1_pin3), .pin13(a_2), .pin12(c_2), .pin11(n7408_1_pin11),
    .pin10(n7408_1_pin11), .pin9(n7400_1_pin3), .pin8(n7408_1_pin8));  // open: pin4, pin5, pin6
  _7432 #(.ShowInternalStructure("true")) u_7432_1 (
    .pin13(n7402_1_pin13), .pin12(n7408_1_pin3), .pin11(n7432_1_pin11), .pin10(n7432_1_pin11),
    .pin9(n7408_1_pin8), .pin8(out_8));  // open: pin1, pin2, pin3, pin4, pin5, pin6

  // Notes on the sheet:
  //   a'c'
  //   ab'c
  //   bc
endmodule
