// Logisim project Problem_2.circ as structural Verilog: 1 circuit, main circuit main
module main (
  input  _0,
  input  _1,
  input  _2,
  input  _3,
  input  _4,
  input  _5,
  input  _6
);

  wire and_1_out, and_2_out, and_3_out, and_4_out, and_5_out, and_6_out, and_7_out, not_1_out, not_2_out,
       not_3_out, or_1_out, or_2_out, or_3_out, or_4_out, or_5_out, or_6_out, or_7_out, or_8_out, or_9_out,
       or_10_out;

  or or_1 (or_1_out, _3, _4, _5, _6);
  or or_2 (or_2_out, _1, _2, _5, _6);
  or or_3 (or_3_out, _6, _4, _2, _0);
  not not_1 (not_1_out, or_1_out);
  not not_2 (not_2_out, or_2_out);
  not not_3 (not_3_out, or_3_out);
  and and_1 (and_1_out, not_1_out, not_2_out, or_3_out);
  and and_2 (and_2_out, or_2_out, not_3_out, not_1_out);
  and and_3 (and_3_out, not_1_out, or_2_out, or_3_out);
  and and_4 (and_4_out, or_1_out, not_2_out, not_3_out);
  and and_5 (and_5_out, or_1_out, not_2_out, or_3_out);
  and and_6 (and_6_out, or_1_out, or_2_out, not_3_out);
  and and_7 (and_7_out, or_1_out, or_3_out, or_2_out);
  or or_4 (or_4_out, and_1_out, and_3_out, and_4_out, and_6_out);
  or or_5 (or_5_out, and_1_out, and_2_out, and_5_out, and_3_out, and_4_out);
  or or_6 (or_6_out, and_1_out, and_4_out, and_2_out, and_5_out, and_6_out, and_7_out);
  or or_7 (or_7_out, and_3_out, and_4_out, and_1_out, and_6_out, and_7_out);
  or or_8 (or_8_out, and_1_out, and_7_out, and_3_out);
  or or_9 (or_9_out, and_1_out, and_6_out, and_5_out, and_7_out);
  or or_10 (or_10_out, and_3_out, and_4_out, and_6_out, and_5_out, and_7_out);
  _7_Segment_Display u_7_segment_display_1 (
    .g(or_10_out), .f(or_9_out), .a(or_4_out), .b(or_5_out), .e(or_8_out), .d(or_7_out), .c(or_6_out));  // open: dp

  // Notes on the sheet:
  //   A
  //   B
  //   C
  //   car 3
  //   car 6
  //   car 0
  //   car1
  //   car 2
  //   car 4
  //   car 5
  //   A
  //   B
  //   C
  //   D
  //   E
  //   F
  //   G
endmodule
