// Logisim project D_Latch.circ as structural Verilog: 2 circuits, main circuit main
module main (
  input  D,
  input  C,
  output out_3
);

  wire nand_1_out, nand_2_out, nand_4_out, not_1_out;

  not not_1 (not_1_out, D);
  nand nand_1 (nand_1_out, D, C);
  nand nand_2 (nand_2_out, C, not_1_out);
  nand nand_3 (out_3, nand_4_out, nand_1_out);
  nand nand_4 (nand_4_out, out_3, nand_2_out);
endmodule

module D_Flipflop (
  input  in_1,
  output out_2
);

  wire clock_1_out, main_1_out_3, not_1_out;

  Clock clock_1 (.out(clock_1_out));
  main main_1 (.D(in_1), .C(clock_1_out), .out_3(main_1_out_3));
  not not_1 (not_1_out, clock_1_out);
  main main_2 (.D(main_1_out_3), .C(not_1_out), .out_3(out_2));
endmodule
