// Logisim project prob_2.circ as structural Verilog: 1 circuit, main circuit main
module main (
);

  wire and_1_out, and_2_out, and_3_out, and_4_out, and_5_out, button_1_out, clock_1_out, d_ff_1_q, d_ff_2_q,
       not_1_out, not_2_out, not_3_out, or_1_out, or_2_out;

  Button button_1 (.out(button_1_out));
  Clock clock_1 (.out(clock_1_out));
  not not_1 (not_1_out, button_1_out);
  not not_2 (not_2_out, d_ff_1_q);
  D_Flip_Flop d_ff_1 (.D(button_1_out), .clk(clock_1_out), .Q(d_ff_1_q));  // open: Qn, preset, reset
  not not_3 (not_3_out, d_ff_2_q);
  D_Flip_Flop d_ff_2 (.D(or_2_out), .clk(clock_1_out), .Q(d_ff_2_q));  // open: Qn, preset, reset
  and and_1 (and_1_out, d_ff_1_q, not_3_out);
  and and_2 (and_2_out, d_ff_2_q, not_2_out);
  and and_3 (and_3_out, d_ff_1_q, not_3_out, not_1_out);
  and and_4 (and_4_out, not_1_out, d_ff_2_q, not_2_out);
  and and_5 (and_5_out, d_ff_2_q, button_1_out);
  or or_1 (or_1_out, and_1_out, and_2_out);
  or or_2 (or_2_out, and_3_out, and_4_out, and_5_out);
  LED led_1 (.in(or_1_out));

  // Notes on the sheet:
  //   It would also need a quad 2-input or gate which is the 7432 circuit. 
  //   led
  //   n1
  //   n0
  //   This circuit would need 2 7408 quad-input and gates for the states and led. 
  //   Lastly, for the NOT gates, we would need to use the 7404 hex inverter to create NOT gates.
endmodule
