// Logisim project prob_3.circ as structural Verilog: 1 circuit, main circuit main
module main (
  input  [2:0] in_1,
  input  A3,
  input  enable
);

  wire clock_1_out, decoder_1_out0, decoder_1_out1, decoder_1_out2, decoder_1_out3, decoder_1_out4,
       decoder_1_out5, decoder_1_out6, register_1_q, register_2_q, register_3_q, register_4_q, register_5_q,
       register_6_q, register_7_q;

  Decoder #(.select(3)) decoder_1 (
    .out0(decoder_1_out0), .out1(decoder_1_out1), .out2(decoder_1_out2), .out3(decoder_1_out3),
    .out4(decoder_1_out4), .out5(decoder_1_out5), .out6(decoder_1_out6), .sel(in_1), .en(enable));  // open: out7
  Clock clock_1 (.out(clock_1_out));
  Register #(.width(1)) register_1 (.D(A3), .en(decoder_1_out0), .clk(clock_1_out), .Q(register_1_q));  // open: clr
  Register #(.width(1)) register_2 (.D(A3), .en(decoder_1_out1), .clk(clock_1_out), .Q(register_2_q));  // open: clr
  Register #(.width(1)) register_3 (.D(A3), .en(decoder_1_out2), .clk(clock_1_out), .Q(register_3_q));  // open: clr
  Register #(.width(1)) register_4 (.D(A3), .en(decoder_1_out3), .clk(clock_1_out), .Q(register_4_q));  // open: clr
  Register #(.width(1)) register_5 (.D(A3), .en(decoder_1_out4), .clk(clock_1_out), .Q(register_5_q));  // open: clr
  Register #(.width(1)) register_6 (.D(A3), .en(decoder_1_out5), .clk(clock_1_out), .Q(register_6_q));  // open: clr
  Register #(.width(1)) register_7 (.D(A3), .en(decoder_1_out6), .clk(clock_1_out), .Q(register_7_q));  // open: clr

  // Notes on the sheet:
  //   actuator
  //   gets the actuator
  //   a/c
  //   d0
  //   d1
  //   d2
  //   d3
  //   engine
  //   wipers
endmodule
