// Logisim project 8_bit_sub.circ as structural Verilog: 2 circuits, main circuit main
module main (
  input  b_in,
  input  a,
  input  b,
  output out_4,
  output out_5
);

  wire and_1_out, and_2_out, not_1_out, not_2_out, xor_1_out;

  not not_1 (not_1_out, a);
  xor xor_1 (xor_1_out, a, b);
  and and_1 (and_1_out, b, not_1_out);
  not not_2 (not_2_out, xor_1_out);
  xor xor_2 (out_4, b_in, xor_1_out);
  and and_2 (and_2_out, not_2_out, b_in);
  or or_1 (out_5, and_2_out, and_1_out);

  // Notes on the sheet:
  //   out
  //   b_out
endmodule

module eight_bit_subtractor (
  input  in_1,
  input  in_2,
  input  in_3,
  input  in_4,
  input  in_5,
  input  in_6,
  input  in_7,
  input  in_8,
  input  in_9,
  input  in_10,
  input  in_11,
  input  in_12,
  input  in_13,
  input  in_14,
  input  in_15,
  input  in_16,
  output out_17,
  output out_18,
  output out_19,
  output out_20,
  output out_21,
  output out_22,
  output out_23,
  output out_24,
  output out_25
);

  wire main_2_out_5, main_3_out_5, main_4_out_5, main_5_out_5, main_6_out_5, main_7_out_5, main_8_out_5;

  main main_1 (.b_in(main_2_out_5), .a(in_2), .b(in_1), .out_4(out_18), .out_5(out_17));
  main main_2 (.b_in(main_3_out_5), .a(in_4), .b(in_3), .out_4(out_19), .out_5(main_2_out_5));
  main main_3 (.b_in(main_4_out_5), .a(in_6), .b(in_5), .out_4(out_20), .out_5(main_3_out_5));
  main main_4 (.b_in(main_5_out_5), .a(in_8), .b(in_7), .out_4(out_21), .out_5(main_4_out_5));
  main main_5 (.b_in(main_6_out_5), .a(in_10), .b(in_9), .out_4(out_22), .out_5(main_5_out_5));
  main main_6 (.b_in(main_7_out_5), .a(in_12), .b(in_11), .out_4(out_23), .out_5(main_6_out_5));
  main main_7 (.b_in(main_8_out_5), .a(in_14), .b(in_13), .out_4(out_24), .out_5(main_7_out_5));
  main main_8 (.a(in_16), .b(in_15), .out_4(out_25), .out_5(main_8_out_5));  // open: b_in

  // Notes on the sheet:
  //   s7
  //   b_out
endmodule
