// Logisim project problem2.circ as structural Verilog: 7 circuits, main circuit main
module main (
  input  a,
  input  b,
  input  cin,
  output sum,
  output cout
);

  wire and_1_out, and_2_out, xor_1_out;

  xor xor_1 (xor_1_out, a, b);
  xor xor_2 (sum, xor_1_out, cin);
  and and_1 (and_1_out, xor_1_out, cin);
  and and_2 (and_2_out, b, a);
  or or_1 (cout, and_1_out, and_2_out);
endmodule

module eight_bit_adder (
  input  b7,
  input  a7,
  input  b6,
  input  a6,
  input  b5,
  input  a5,
  input  b4,
  input  a4,
  input  b3,
  input  a3,
  input  in_11,
  input  a2,
  input  b2,
  input  a1,
  input  b0,
  input  a0,
  input  c_in,
  output c_out,
  output s7,
  output s6,
  output s5,
  output s4,
  output s3,
  output s2,
  output s1,
  output s0
);

  wire main_2_cout, main_3_cout, main_4_cout, main_5_cout, main_6_cout, main_7_cout, main_8_cout;

  main main_1 (.a(a7), .b(b7), .cin(main_2_cout), .sum(s7), .cout(c_out));
  main main_2 (.a(a6), .b(b6), .cin(main_3_cout), .sum(s6), .cout(main_2_cout));
  main main_3 (.a(a5), .b(b5), .cin(main_4_cout), .sum(s5), .cout(main_3_cout));
  main main_4 (.a(a4), .b(b4), .cin(main_5_cout), .sum(s4), .cout(main_4_cout));
  main main_5 (.a(a3), .b(b3), .cin(main_6_cout), .sum(s3), .cout(main_5_cout));
  main main_6 (.a(a2), .b(in_11), .cin(main_7_cout), .sum(s2), .cout(main_6_cout));
  main main_7 (.a(a1), .b(b2), .cin(main_8_cout), .sum(s1), .cout(main_7_cout));
  main main_8 (.a(a0), .b(b0), .cin(c_in), .sum(s0), .cout(main_8_cout));
endmodule

module eight_bit_sub (
  input  in_1,
  input  in_2,
  input  in_3,
  input  in_4,
  input  in_5,
  input  in_6,
  input  in_7,
  input  in_8,
  input  in_9,
  input  in_10,
  input  in_11,
  input  in_12,
  input  in_13,
  input  in_14,
  input  in_15,
  input  in_16
);

  wire eight_bit_adder_1_c_out, eight_bit_adder_1_s0, eight_bit_adder_1_s1, eight_bit_adder_1_s2,
       eight_bit_adder_1_s3, eight_bit_adder_1_s4, eight_bit_adder_1_s5, eight_bit_adder_1_s6,
       eight_bit_adder_1_s7, not_1_out, not_2_out, not_3_out, not_4_out, not_5_out, not_6_out, not_7_out,
       not_8_out;

  not not_1 (not_1_out, in_1);
  not not_2 (not_2_out, in_2);
  not not_3 (not_3_out, in_3);
  not not_4 (not_4_out, in_4);
  LED led_1 (.in(eight_bit_adder_1_s0));
  not not_5 (not_5_out, in_5);
  not not_6 (not_6_out, in_6);
  LED led_2 (.in(eight_bit_adder_1_s1));
  LED led_3 (.in(eight_bit_adder_1_s2));
  LED led_4 (.in(eight_bit_adder_1_s3));
  LED led_5 (.in(eight_bit_adder_1_s4));
  not not_7 (not_7_out, in_7);
  not not_8 (not_8_out, in_8);
  LED led_6 (.in(eight_bit_adder_1_s5));
  LED led_7 (.in(eight_bit_adder_1_s6));
  LED led_8 (.in(eight_bit_adder_1_s7));
  LED led_9 (.in(eight_bit_adder_1_c_out));
  eight_bit_adder eight_bit_adder_1 (
    .b7(not_8_out), .a7(in_16), .b6(not_7_out), .a6(in_15), .b5(not_6_out), .a5(in_14), .b4(not_5_out),
    .a4(in_13), .b3(not_4_out), .a3(in_12), .in_11(not_3_out), .a2(in_11), .b2(not_2_out), .a1(in_10),
    .b0(not_1_out), .a0(in_9), .c_in(1'b1), .c_out(eight_bit_adder_1_c_out), .s7(eight_bit_adder_1_s7),
    .s6(eight_bit_adder_1_s6), .s5(eight_bit_adder_1_s5), .s4(eight_bit_adder_1_s4),
    .s3(eight_bit_adder_1_s3), .s2(eight_bit_adder_1_s2), .s1(eight_bit_adder_1_s1), .s0(eight_bit_adder_1_s0));
endmodule

module eight_bit_shifter (
  input  i0,
  input  i1,
  input  i2,
  input  i3,
  input  i4,
  input  i5,
  input  i6,
  input  i7,
  input  r_l,
  input  enable,
  output s5,
  output s7,
  output s1,
  output s0,
  output s2,
  output s4,
  output s6,
  output s3
);

  wire and_1_out, and_2_out, and_3_out, and_4_out, and_5_out, and_6_out, and_7_out, and_8_out, and_9_out,
       and_10_out, and_11_out, and_12_out, and_13_out, and_14_out, not_1_out, or_1_out, or_2_out, or_3_out,
       or_4_out, or_5_out, or_6_out;

  not not_1 (not_1_out, r_l);
  and and_1 (and_1_out, i0, r_l);
  Multiplexer multiplexer_1 (.in0(i0), .in1(and_2_out), .out(s0), .sel(enable));
  and and_2 (and_2_out, i1, not_1_out);
  or or_1 (or_1_out, and_1_out, and_4_out);
  Multiplexer multiplexer_2 (.in0(i1), .in1(or_1_out), .out(s1), .sel(enable));
  and and_3 (and_3_out, i1, r_l);
  and and_4 (and_4_out, i2, not_1_out);
  or or_2 (or_2_out, and_3_out, and_6_out);
  Multiplexer multiplexer_3 (.in0(i2), .in1(or_2_out), .out(s2), .sel(enable));
  and and_5 (and_5_out, i2, r_l);
  and and_6 (and_6_out, i3, not_1_out);
  and and_7 (and_7_out, i3, r_l);
  or or_3 (or_3_out, and_5_out, and_8_out);
  Multiplexer multiplexer_4 (.in0(i3), .in1(or_3_out), .out(s3), .sel(enable));
  and and_8 (and_8_out, i4, not_1_out);
  or or_4 (or_4_out, and_7_out, and_10_out);
  Multiplexer multiplexer_5 (.in0(i4), .in1(or_4_out), .out(s4), .sel(enable));
  and and_9 (and_9_out, i4, r_l);
  or or_5 (or_5_out, and_9_out, and_12_out);
  Multiplexer multiplexer_6 (.in0(i5), .in1(or_5_out), .out(s5), .sel(enable));
  and and_10 (and_10_out, i5, not_1_out);
  and and_11 (and_11_out, i5, r_l);
  or or_6 (or_6_out, and_11_out, and_14_out);
  Multiplexer multiplexer_7 (.in0(i6), .in1(or_6_out), .out(s6), .sel(enable));
  and and_12 (and_12_out, i6, not_1_out);
  and and_13 (and_13_out, i6, r_l);
  and and_14 (and_14_out, not_1_out, i7);
  Multiplexer multiplexer_8 (.in0(i7), .in1(and_13_out), .out(s7), .sel(enable));

  // Notes on the sheet:
  //   d=0, shift right
endmodule

module eight_bit_shifter_two (
  input  i0,
  input  i1,
  input  i2,
  input  i3,
  input  i4,
  input  i5,
  input  i6,
  input  i7,
  input  r_l,
  input  enable,
  output s0,
  output s1,
  output s2,
  output s3,
  output s4,
  output s5,
  output s6,
  output s7
);

  wire eight_bit_shifter_1_s0, eight_bit_shifter_1_s1, eight_bit_shifter_1_s2, eight_bit_shifter_1_s3,
       eight_bit_shifter_1_s4, eight_bit_shifter_1_s5, eight_bit_shifter_1_s6, eight_bit_shifter_1_s7;

  eight_bit_shifter eight_bit_shifter_1 (
    .i0(i0), .i1(i1), .i2(i2), .i3(i3), .i4(i4), .i5(i5), .i6(i6), .i7(i7), .r_l(r_l), .enable(enable),
    .s5(eight_bit_shifter_1_s5), .s7(eight_bit_shifter_1_s7), .s1(eight_bit_shifter_1_s1),
    .s0(eight_bit_shifter_1_s0), .s2(eight_bit_shifter_1_s2), .s4(eight_bit_shifter_1_s4),
    .s6(eight_bit_shifter_1_s6), .s3(eight_bit_shifter_1_s3));
  eight_bit_shifter eight_bit_shifter_2 (
    .i0(eight_bit_shifter_1_s0), .i1(eight_bit_shifter_1_s1), .i2(eight_bit_shifter_1_s2),
    .i3(eight_bit_shifter_1_s3), .i4(eight_bit_shifter_1_s4), .i5(eight_bit_shifter_1_s5),
    .i6(eight_bit_shifter_1_s6), .i7(eight_bit_shifter_1_s7), .r_l(r_l), .enable(enable), .s5(s5), .s7(s7),
    .s1(s1), .s0(s0), .s2(s2), .s4(s4), .s6(s6), .s3(s1));

  assign s3 = s1;
endmodule

module eight_bit_shifter_four (
  input  i0,
  input  i1,
  input  i2,
  input  i3,
  input  i4,
  input  i5,
  input  i6,
  input  i7,
  input  r_l,
  input  enable,
  output s0,
  output s1,
  output s2,
  output s3,
  output s4,
  output s5,
  output s6,
  output s7
);

  wire eight_bit_shifter_two_1_s0, eight_bit_shifter_two_1_s1, eight_bit_shifter_two_1_s2,
       eight_bit_shifter_two_1_s3, eight_bit_shifter_two_1_s4, eight_bit_shifter_two_1_s5,
       eight_bit_shifter_two_1_s6, eight_bit_shifter_two_1_s7;

  eight_bit_shifter_two eight_bit_shifter_two_1 (
    .i0(i0), .i1(i1), .i2(i2), .i3(i3), .i4(i4), .i5(i5), .i6(i6), .i7(i7), .r_l(r_l), .enable(enable),
    .s0(eight_bit_shifter_two_1_s0), .s1(eight_bit_shifter_two_1_s1), .s2(eight_bit_shifter_two_1_s2),
    .s3(eight_bit_shifter_two_1_s3), .s4(eight_bit_shifter_two_1_s4), .s5(eight_bit_shifter_two_1_s5),
    .s6(eight_bit_shifter_two_1_s6), .s7(eight_bit_shifter_two_1_s7));
  eight_bit_shifter_two eight_bit_shifter_two_2 (
    .i0(eight_bit_shifter_two_1_s0), .i1(eight_bit_shifter_two_1_s1), .i2(eight_bit_shifter_two_1_s2),
    .i3(eight_bit_shifter_two_1_s3), .i4(eight_bit_shifter_two_1_s4), .i5(eight_bit_shifter_two_1_s5),
    .i6(eight_bit_shifter_two_1_s6), .i7(eight_bit_shifter_two_1_s7), .r_l(r_l), .enable(enable), .s0(s0),
    .s1(s1), .s2(s2), .s3(s3), .s4(s4), .s5(s5), .s6(s6), .s7(s7));
endmodule

module barrel_shift_right (
  input  x,
  input  in_2,
  input  in_3,
  input  in_4,
  input  in_5,
  input  in_6,
  input  in_7,
  input  in_8,
  input  in_9,
  input  y,
  input  z
);

  wire eight_bit_shifter_four_1_s0, eight_bit_shifter_four_1_s1, eight_bit_shifter_four_1_s2,
       eight_bit_shifter_four_1_s3, eight_bit_shifter_four_1_s4, eight_bit_shifter_four_1_s5,
       eight_bit_shifter_four_1_s6, eight_bit_shifter_four_1_s7, eight_bit_shifter_two_1_s0,
       eight_bit_shifter_two_1_s1, eight_bit_shifter_two_1_s2, eight_bit_shifter_two_1_s3,
       eight_bit_shifter_two_1_s4, eight_bit_shifter_two_1_s5, eight_bit_shifter_two_1_s6,
       eight_bit_shifter_two_1_s7;

  eight_bit_shifter_four eight_bit_shifter_four_1 (
    .i0(in_9), .i1(in_8), .i2(in_7), .i3(in_6), .i4(in_5), .i5(in_4), .i6(in_3), .i7(in_2), .r_l(1'b0),
    .enable(x), .s0(eight_bit_shifter_four_1_s0), .s1(eight_bit_shifter_four_1_s1),
    .s2(eight_bit_shifter_four_1_s2), .s3(eight_bit_shifter_four_1_s3), .s4(eight_bit_shifter_four_1_s4),
    .s5(eight_bit_shifter_four_1_s5), .s6(eight_bit_shifter_four_1_s6), .s7(eight_bit_shifter_four_1_s7));
  eight_bit_shifter_two eight_bit_shifter_two_1 (
    .i0(eight_bit_shifter_four_1_s0), .i1(eight_bit_shifter_four_1_s1), .i2(eight_bit_shifter_four_1_s2),
    .i3(eight_bit_shifter_four_1_s3), .i4(eight_bit_shifter_four_1_s4), .i5(eight_bit_shifter_four_1_s5),
    .i6(eight_bit_shifter_four_1_s6), .i7(eight_bit_shifter_four_1_s7), .r_l(1'b0), .enable(y),
    .s0(eight_bit_shifter_two_1_s0), .s1(eight_bit_shifter_two_1_s1), .s2(eight_bit_shifter_two_1_s2),
    .s3(eight_bit_shifter_two_1_s3), .s4(eight_bit_shifter_two_1_s4), .s5(eight_bit_shifter_two_1_s5),
    .s6(eight_bit_shifter_two_1_s6), .s7(eight_bit_shifter_two_1_s7));
  eight_bit_shifter eight_bit_shifter_1 (
    .i0(eight_bit_shifter_two_1_s0), .i1(eight_bit_shifter_two_1_s1), .i2(eight_bit_shifter_two_1_s2),
    .i3(eight_bit_shifter_two_1_s3), .i4(eight_bit_shifter_two_1_s4), .i5(eight_bit_shifter_two_1_s5),
    .i6(eight_bit_shifter_two_1_s6), .i7(eight_bit_shifter_two_1_s7), .r_l(1'b0), .enable(z));  // open: s5, s7, s1, s0, s2, s4, s6, s3

  // Notes on the sheet:
  //   0 for shift right
endmodule
