// Logisim project cpu_with_subtract_fix.circ as structural Verilog: 27 circuits, main circuit CPU
module CPU (
  output [63:0] ValP,
  output [63:0] ValC,
  output [3:0] ifun,
  output [3:0] icode,
  output [63:0] ValE,
  output [63:0] ValA,
  output condition,
  output [63:0] ValB,
  output [63:0] PC,
  output [63:0] ValM,
  output [3:0] rA,
  output [3:0] rB,
  output [7:0] out_13,
  output [7:0] out_14,
  output [63:0] out_15,
  output [63:0] out_16,
  output [63:0] out_17,
  output [63:0] out_18,
  output [63:0] out_19,
  output [63:0] out_20,
  output [63:0] pcc,
  output [63:0] out_22,
  output [63:0] out_23,
  output [63:0] out_24,
  output [63:0] out_25,
  output [63:0] out_26,
  output [63:0] out_27,
  output [63:0] out_28,
  output [63:0] out_29,
  output [63:0] out_30
);

  wire clock_1_out, comparator_1_eq, comparator_2_eq, controlled_buffer_1_out, not_1_out, or_1_out;
  wire [3:0] decoder_dste_1_dste, decoder_dstm_1_dstm;

  or or_1 (or_1_out, not_1_out, comparator_1_eq);
  Clock clock_1 (.out(clock_1_out));
  assign controlled_buffer_1_out = or_1_out ? clock_1_out : 1'bz;  // Controlled_Buffer controlled_buffer_1
  not not_1 (not_1_out, comparator_2_eq);
  Comparator #(.mode("unsigned"), .width(64)) comparator_1 (
    .a(PC), .b({64{1'b0}}), .eq(comparator_1_eq));  // open: gt, lt
  cycle_20 cycle_20_1 (.Clk(controlled_buffer_1_out), .Cycle_Count(out_13));
  Comparator #(.mode("unsigned"), .width(4)) comparator_2 (
    .a(icode), .b(4'b0000), .eq(comparator_2_eq));  // open: gt, lt
  fetch_main fetch_main_1 (
    .clk(controlled_buffer_1_out), .PC(PC), .cycle(out_13), .icode(icode), .ifun(ifun), .rA(rA), .rB(rB),
    .ValC(ValC), .ValP(ValP));
  decoder_DSTE decoder_dste_1 (.icode(icode), .AddressE(rB), .dstE(decoder_dste_1_dste));
  Decoder_DSTM decoder_dstm_1 (.icode(icode), .Address_M(rA), .dstM(decoder_dstm_1_dstm));
  decoder_register decoder_register_1 (
    .ValE(ValE), .ValM(ValM), .dstE(decoder_dste_1_dste), .srcA(rA), .dstM(decoder_dstm_1_dstm), .srcB(rB),
    .icode(icode), .Cycle_counter(out_13), .Clk(controlled_buffer_1_out), .ValA(ValA), .ValB(ValB),
    .rax(out_15), .rcx(out_16), .rdx(out_17), .rbx(out_18), .rsp(out_19), .rbp(out_20), .rsi(out_22),
    .rdi(out_23), .r8(out_24), .r9(out_25), .r10(out_26), .r11(out_27), .r12(out_28), .r13(out_29),
    .r14(out_30));
  execute execute_1 (
    .cyc_cnt(out_13), .clk(controlled_buffer_1_out), .icode(icode), .ifun(ifun), .valC(ValC), .valA(ValA),
    .valB(ValB), .condition(condition), .valE(ValE));
  mainMem mainmem_1 (
    .icode(icode), .ValE(ValE), .ValA(ValA), .ValP(ValP), .Clk(controlled_buffer_1_out),
    .cycle_count(out_13), .ValM(ValM));
  New_PC new_pc_1 (
    .cycle(out_13), .cnd(condition), .icode(icode), .ValC(ValC), .ValM(ValM), .ValP(ValP),
    .clk(controlled_buffer_1_out), .pc_new(PC));

  assign out_14 = out_13;
  assign pcc = PC;

  // Notes on the sheet:
  //   rA -> Address E
  //   rB -> AddressM
  //   rA -> srcA
  //   rB -> srcB
endmodule

module fetch_main (
  input  clk,
  input  [63:0] PC,
  input  [7:0] cycle,
  output [3:0] icode,
  output [3:0] ifun,
  output [3:0] rA,
  output [3:0] rB,
  output [63:0] ValC,
  output [63:0] ValP
);

  wire comparator_1_gt, controlled_buffer_1_out, need_regids_1_needs_register, need_valc_1_needs_valc,
       not_1_out;
  wire [7:0] fetch_instruction_memory_1_s1, fetch_instruction_memory_1_s2, fetch_instruction_memory_1_s3,
       fetch_instruction_memory_1_s4, fetch_instruction_memory_1_s5, fetch_instruction_memory_1_s6,
       fetch_instruction_memory_1_s7, fetch_instruction_memory_1_s8, fetch_instruction_memory_1_s9;
  wire [11:0] pc_increment_1_valp;

  fetch_instruction_memory fetch_instruction_memory_1 (
    .PC(PC[11:0]), .cycle(cycle), .clk(controlled_buffer_1_out), .s0({icode, ifun}),
    .s1(fetch_instruction_memory_1_s1), .s2(fetch_instruction_memory_1_s2),
    .s3(fetch_instruction_memory_1_s3), .s4(fetch_instruction_memory_1_s4),
    .s5(fetch_instruction_memory_1_s5), .s6(fetch_instruction_memory_1_s6),
    .s7(fetch_instruction_memory_1_s7), .s8(fetch_instruction_memory_1_s8), .s9(fetch_instruction_memory_1_s9));
  fetch_allign fetch_allign_1 (
    .Byte1(fetch_instruction_memory_1_s1), .Byte2(fetch_instruction_memory_1_s2),
    .Byte3(fetch_instruction_memory_1_s3), .Byte4(fetch_instruction_memory_1_s4),
    .Byte5(fetch_instruction_memory_1_s5), .Byte6(fetch_instruction_memory_1_s6),
    .Byte7(fetch_instruction_memory_1_s7), .Byte8(fetch_instruction_memory_1_s8),
    .Byte9(fetch_instruction_memory_1_s9), .needs_register(need_regids_1_needs_register), .R_A(rA), .R_B(rB),
    .valc(ValC));
  Comparator #(.mode("unsigned")) comparator_1 (.a(cycle), .b(8'ha), .gt(comparator_1_gt));  // open: eq, lt
  assign controlled_buffer_1_out = not_1_out ? clk : 1'bz;  // Controlled_Buffer controlled_buffer_1
  not not_1 (not_1_out, comparator_1_gt);
  need_regids need_regids_1 (.icode(icode), .needs_register(need_regids_1_needs_register));
  need_valC need_valc_1 (.icode(icode), .needs_ValC(need_valc_1_needs_valc));
  assign ValP = {{52{pc_increment_1_valp[11]}}, pc_increment_1_valp};  // Bit_Extender bit_extender_1
  pc_increment pc_increment_1 (
    .need_reg(need_regids_1_needs_register), .imm_value(need_valc_1_needs_valc), .PC(PC[11:0]),
    .ValP(pc_increment_1_valp));

  // Notes on the sheet:
  //   splits the first byte
endmodule

module fetch_instruction_memory (
  input  [11:0] PC,
  input  [7:0] cycle,
  input  clk,
  output [7:0] s0,
  output [7:0] s1,
  output [7:0] s2,
  output [7:0] s3,
  output [7:0] s4,
  output [7:0] s5,
  output [7:0] s6,
  output [7:0] s7,
  output [7:0] s8,
  output [7:0] s9
);

  wire comparator_1_gt, decoder_1_out0, decoder_1_out1, decoder_1_out2, decoder_1_out3, decoder_1_out4,
       decoder_1_out5, decoder_1_out6, decoder_1_out7, decoder_1_out8, decoder_1_out9;
  wire [7:0] demultiplexer_1_out0, demultiplexer_1_out1, demultiplexer_1_out2, demultiplexer_1_out3,
       demultiplexer_1_out4, demultiplexer_1_out5, demultiplexer_1_out6, demultiplexer_1_out7,
       demultiplexer_1_out8, demultiplexer_1_out9, multiplexer_1_out, rom_1_data;
  wire [11:0] adder_1_out, bit_extender_1_out;

  Clock clock_1 ();  // open: out
  Multiplexer #(.width(8)) multiplexer_1 (.in0(8'h9), .in1(cycle), .out(multiplexer_1_out), .sel(comparator_1_gt));
  Comparator #(.mode("unsigned")) comparator_1 (.a(8'ha), .b(cycle), .gt(comparator_1_gt));  // open: eq, lt
  assign bit_extender_1_out = {{4{multiplexer_1_out[7]}}, multiplexer_1_out};  // Bit_Extender bit_extender_1
  Adder #(.width(12)) adder_1 (.a(PC), .b(bit_extender_1_out), .out(adder_1_out));  // open: cin, cout
  ROM #(.addrWidth(12)) rom_1 (.addr(adder_1_out), .data(rom_1_data));
  Demultiplexer #(.select(4), .width(8)) demultiplexer_1 (
    .out0(demultiplexer_1_out0), .out1(demultiplexer_1_out1), .out2(demultiplexer_1_out2),
    .out3(demultiplexer_1_out3), .out4(demultiplexer_1_out4), .out5(demultiplexer_1_out5),
    .out6(demultiplexer_1_out6), .out7(demultiplexer_1_out7), .out8(demultiplexer_1_out8),
    .out9(demultiplexer_1_out9), .in(rom_1_data), .sel(multiplexer_1_out[3:0]));  // open: out10, out11, out12, out13, out14, out15
  Decoder #(.enable("false"), .select(4)) decoder_1 (
    .out0(decoder_1_out0), .out1(decoder_1_out1), .out2(decoder_1_out2), .out3(decoder_1_out3),
    .out4(decoder_1_out4), .out5(decoder_1_out5), .out6(decoder_1_out6), .out7(decoder_1_out7),
    .out8(decoder_1_out8), .out9(decoder_1_out9), .sel(multiplexer_1_out[3:0]));  // open: out10, out11, out12, out13, out14, out15
  Register register_1 (.D(demultiplexer_1_out0), .en(decoder_1_out0), .clk(clk), .Q(s0));  // open: clr
  Register register_2 (.D(demultiplexer_1_out1), .en(decoder_1_out1), .clk(clk), .Q(s1));  // open: clr
  Register register_3 (.D(demultiplexer_1_out2), .en(decoder_1_out2), .clk(clk), .Q(s2));  // open: clr
  Register register_4 (.D(demultiplexer_1_out3), .en(decoder_1_out3), .clk(clk), .Q(s3));  // open: clr
  Register register_5 (.D(demultiplexer_1_out4), .en(decoder_1_out4), .clk(clk), .Q(s4));  // open: clr
  Register register_6 (.D(demultiplexer_1_out5), .en(decoder_1_out5), .clk(clk), .Q(s5));  // open: clr
  Register register_7 (.D(demultiplexer_1_out6), .en(decoder_1_out6), .clk(clk), .Q(s6));  // open: clr
  Register register_8 (.D(demultiplexer_1_out7), .en(decoder_1_out7), .clk(clk), .Q(s7));  // open: clr
  Register register_9 (.D(demultiplexer_1_out8), .en(decoder_1_out8), .clk(clk), .Q(s8));  // open: clr
  Register register_10 (.D(demultiplexer_1_out9), .en(decoder_1_out9), .clk(clk), .Q(s9));  // open: clr

  // Notes on the sheet:
  //   contents of rom_1 (hex, n*v repeats v):
  //   30 f0 8*0 30 f8 8 7*0 30 f1 8*0 30 f2 8*0 30 f3 18 7*0 30 f6 1 7*0 30 f9 28 7*0 40 90 8*0 30 f9 14
  //   7*0 60 80 40 90 8*0 30 f9 5a 7*0 60 80 40 90 8*0 30 f9 1e 7*0 60 80 40 90 8*0 30 f2 8*0 20 14 61 34
  //   73 6 1 6*0 20 39 61 19 50 52 8*0 60 82 50 72 8*0 61 82 20 54 61 74 72 ea 7*0 40 72 8*0 60 82 40 52
  //   8*0 61 82 20 2a 60 82 20 94 61 a4 75 a9 7*0 60 81 70 92 7*0 30 f0 8*0 50 b0 8*0 60 80 50 c0 8*0 60
  //   80 50 d0 8*0 60 80 50 e0
endmodule

module need_regids (
  input  [3:0] icode,
  output needs_register
);

  wire comparator_1_eq, comparator_2_eq, comparator_3_eq, comparator_4_eq, comparator_5_eq, comparator_6_eq,
       comparator_7_eq;

  Comparator #(.mode("unsigned"), .width(4)) comparator_1 (
    .a(icode), .b(4'b0010), .eq(comparator_1_eq));  // open: gt, lt
  Comparator #(.mode("unsigned"), .width(4)) comparator_2 (
    .a(icode), .b(4'b0011), .eq(comparator_2_eq));  // open: gt, lt
  Comparator #(.mode("unsigned"), .width(4)) comparator_3 (
    .a(icode), .b(4'b0100), .eq(comparator_3_eq));  // open: gt, lt
  Comparator #(.mode("unsigned"), .width(4)) comparator_4 (
    .a(icode), .b(4'b0101), .eq(comparator_4_eq));  // open: gt, lt
  Comparator #(.mode("unsigned"), .width(4)) comparator_5 (
    .a(icode), .b(4'b0110), .eq(comparator_5_eq));  // open: gt, lt
  Comparator #(.mode("unsigned"), .width(4)) comparator_6 (
    .a(icode), .b(4'b1010), .eq(comparator_6_eq));  // open: gt, lt
  Comparator #(.mode("unsigned"), .width(4)) comparator_7 (
    .a(icode), .b(4'b1011), .eq(comparator_7_eq));  // open: gt, lt
  or or_1 (needs_register, comparator_1_eq, comparator_2_eq, comparator_3_eq, comparator_4_eq, comparator_5_eq, comparator_6_eq, comparator_7_eq);

  // Notes on the sheet:
  //   rrmovq
  //   irmovq
  //   rmmovq
  //   mrmovq
  //   opl
  //   pushq
  //   popq
endmodule

module need_valC (
  input  [3:0] icode,
  output needs_ValC
);

  wire comparator_1_eq, comparator_2_eq, comparator_3_eq, comparator_4_eq, comparator_5_eq;

  Comparator #(.mode("unsigned"), .width(4)) comparator_1 (
    .a(icode), .b(4'b0011), .eq(comparator_1_eq));  // open: gt, lt
  Comparator #(.mode("unsigned"), .width(4)) comparator_2 (
    .a(icode), .b(4'b0100), .eq(comparator_2_eq));  // open: gt, lt
  Comparator #(.mode("unsigned"), .width(4)) comparator_3 (
    .a(icode), .b(4'b0101), .eq(comparator_3_eq));  // open: gt, lt
  Comparator #(.mode("unsigned"), .width(4)) comparator_4 (
    .a(icode), .b(4'b0111), .eq(comparator_4_eq));  // open: gt, lt
  Comparator #(.mode("unsigned"), .width(4)) comparator_5 (
    .a(icode), .b(4'b1000), .eq(comparator_5_eq));  // open: gt, lt
  or or_1 (needs_ValC, comparator_1_eq, comparator_2_eq, comparator_3_eq, comparator_4_eq, comparator_5_eq);

  // Notes on the sheet:
  //   irmovq
  //   rmmovq
  //   mrmovq
  //   jxx
  //   call
endmodule

module pc_increment (
  input  need_reg,
  input  imm_value,
  input  [11:0] PC,
  output [11:0] ValP
);

  wire adder_1_cout, adder_2_cout;
  wire [11:0] adder_1_out, adder_2_out, multiplexer_1_out, multiplexer_2_out;

  Multiplexer #(.width(12)) multiplexer_1 (.in0({12{1'b0}}), .in1(12'h1), .out(multiplexer_1_out), .sel(need_reg));
  Multiplexer #(.width(12)) multiplexer_2 (.in0({12{1'b0}}), .in1(12'h8), .out(multiplexer_2_out), .sel(imm_value));
  Adder #(.width(12)) adder_1 (.a(multiplexer_2_out), .b(PC), .out(adder_1_out), .cout(adder_1_cout));  // open: cin
  Adder #(.width(12)) adder_2 (
    .a(multiplexer_1_out), .b(adder_1_out), .out(adder_2_out), .cin(adder_1_cout), .cout(adder_2_cout));
  Adder #(.width(12)) adder_3 (.a(adder_2_out), .b(12'h1), .out(ValP), .cin(adder_2_cout));  // open: cout
endmodule

module fetch_allign (
  input  [7:0] Byte1,
  input  [7:0] Byte2,
  input  [7:0] Byte3,
  input  [7:0] Byte4,
  input  [7:0] Byte5,
  input  [7:0] Byte6,
  input  [7:0] Byte7,
  input  [7:0] Byte8,
  input  [7:0] Byte9,
  input  needs_register,
  output [3:0] R_A,
  output [3:0] R_B,
  output [63:0] valc
);

  Multiplexer #(.width(8)) multiplexer_1 (.in1(Byte1), .out({R_A, R_B}), .sel(needs_register));  // open: in0
  Multiplexer #(.width(64)) multiplexer_2 (
    .in0({Byte1, Byte2, Byte3, Byte4, Byte5, Byte6, Byte7, Byte8}),
    .in1({Byte2, Byte3, Byte4, Byte5, Byte6, Byte7, Byte8, Byte9}),
    .out({valc[7:0], valc[15:8], valc[23:16], valc[31:24], valc[39:32], valc[47:40], valc[55:48], valc[63:56]}),
    .sel(needs_register));
endmodule

module main (
  input  [63:0] ValA,
  input  [63:0] ValB,
  output [63:0] ValE,
  output [63:0] ValM,
  output [11:0] out_5,
  output [3:0] ifun,
  output [3:0] icode,
  output [3:0] rA,
  output [3:0] rB,
  output [63:0] ValC,
  output [63:0] ValP,
  output [63:0] rax,
  output [63:0] rcx,
  output [63:0] rdx,
  output [63:0] rbx,
  output [63:0] rsp,
  output [63:0] rbp,
  output [63:0] rsi,
  output [63:0] rdi,
  output [63:0] r8,
  output [63:0] r9,
  output [63:0] r10,
  output [63:0] r11,
  output [63:0] r12,
  output [63:0] r13,
  output [63:0] r14
);

  wire clock_1_out, comparator_1_eq, execute_1_condition;
  wire [3:0] decoder_dste_1_dste, decoder_dstm_1_dstm;
  wire [7:0] adder_1_out, multiplexer_1_out, register_1_q;
  wire [63:12] new_pc_1_pc_new;

  Clock clock_1 (.out(clock_1_out));
  Multiplexer #(.width(8)) multiplexer_1 (
    .in0(adder_1_out), .in1({8{1'b0}}), .out(multiplexer_1_out), .sel(comparator_1_eq));
  Register register_1 (.D(multiplexer_1_out), .clk(clock_1_out), .Q(register_1_q));  // open: en, clr
  Adder adder_1 (.a(register_1_q), .b(8'h1), .out(adder_1_out));  // open: cin, cout
  Comparator #(.mode("unsigned")) comparator_1 (.a(adder_1_out), .b(8'h15), .eq(comparator_1_eq));  // open: gt, lt
  // fetch_main fetch_main_1: pin names not known; wires that end beside it: out_5, clock_1_out, multiplexer_1_out, ifun, icode, rA, rB, ValC, ValP
  Decoder_DSTM decoder_dstm_1 (.icode(icode), .Address_M(rA), .dstM(decoder_dstm_1_dstm));
  decoder_DSTE decoder_dste_1 (.icode(icode), .AddressE(rB), .dstE(decoder_dste_1_dste));
  // decoder_register decoder_register_1: pin names not known; wires that end beside it: ValE, ValM, decoder_dste_1_dste, rA, decoder_dstm_1_dstm, rB, multiplexer_1_out, clock_1_out, ValA, ValB, rax, rcx, rdx, rbx, rsp, rbp, rsi, rdi, r8, r9, r10, r11, r12, r13, r14
  execute execute_1 (
    .cyc_cnt(multiplexer_1_out), .clk(clock_1_out), .icode(icode), .ifun(ifun), .valC(ValC), .valA(ValA),
    .valB(ValB), .condition(execute_1_condition), .valE(ValE));
  mainMem mainmem_1 (
    .icode(icode), .ValE(ValE), .ValA(ValA), .ValP(ValP), .Clk(clock_1_out), .ValM(ValM));  // open: cycle_count
  New_PC new_pc_1 (
    .cycle(multiplexer_1_out), .cnd(execute_1_condition), .icode(ifun), .ValC(ValC), .ValM(ValM),
    .ValP(ValP), .clk(clock_1_out), .pc_new({new_pc_1_pc_new, out_5}));

  // Notes on the sheet:
  //   cycle count
  //   cycle count
  //   srcA & srcB connect to rA and rB??
  //   ValA
  //   ValB
  //   ValE for Execute
  //   ValM for execute
  //   ValM
  //   IS CLOCK NEEDED????
endmodule

module decode_main (
  input  [3:0] in_1,
  input  [3:0] rA,
  input  [3:0] rB,
  input  [7:0] in_4,
  input  Clk,
  output [63:0] valA,
  output [63:0] valB,
  output [63:0] rax,
  output [63:0] rcx,
  output [63:0] rdx,
  output [63:0] rbx,
  output [63:0] rsp,
  output [63:0] rbp,
  output [63:0] rsi,
  output [63:0] rdi,
  output [63:0] r8,
  output [63:0] ValE,
  output [63:0] r9,
  output [63:0] r10,
  output [63:0] out_20,
  output [63:0] r11,
  output [63:0] r12,
  output [63:0] r13,
  output [63:0] r14
);

  wire [3:0] decoder_dste_1_dste, decoder_dstm_1_dstm;

  Decoder_DSTM decoder_dstm_1 (.icode(in_1), .Address_M(rA), .dstM(decoder_dstm_1_dstm));
  decoder_DSTE decoder_dste_1 (.icode(in_1), .AddressE(rB), .dstE(decoder_dste_1_dste));
  // decoder_register decoder_register_1: pin names not known; wires that end beside it: ValE, out_20, decoder_dste_1_dste, rA, decoder_dstm_1_dstm, rB, in_4, Clk, valA, valB, rax, rcx, rdx, rbx, rsp, rbp, rsi, rdi, r8, r9, r10, r11, r12, r13, r14

  // Notes on the sheet:
  //   icode
  //   ValM
  //   Cycle_Count
endmodule

module decoder_DSTE (
  input  [3:0] icode,
  input  [3:0] AddressE,
  output [3:0] dstE
);

  wire decoder_1_out2, decoder_1_out3, decoder_1_out6, or_1_out;

  Decoder #(.select(4)) decoder_1 (
    .out2(decoder_1_out2), .out3(decoder_1_out3), .out6(decoder_1_out6), .sel(icode));  // open: out0, out1, out4, out5, out7, out8, out9, out10, out11, out12, out13, out14, out15, en
  or or_1 (or_1_out, decoder_1_out3, decoder_1_out6, decoder_1_out2);
  Multiplexer #(.width(4)) multiplexer_1 (.in0(4'b1111), .in1(AddressE), .out(dstE), .sel(or_1_out));

  // Notes on the sheet:
  //   cmovvXX instruction placed at 2
  //   0xF
endmodule

module Decoder_DSTM (
  input  [3:0] icode,
  input  [3:0] Address_M,
  output [3:0] dstM
);

  wire decoder_1_out5, decoder_1_out11, or_1_out;

  Decoder #(.select(4)) decoder_1 (
    .out5(decoder_1_out5), .out11(decoder_1_out11), .sel(icode));  // open: out0, out1, out2, out3, out4, out6, out7, out8, out9, out10, out12, out13, out14, out15, en
  or or_1 (or_1_out, decoder_1_out5, decoder_1_out11);
  Multiplexer #(.width(4)) multiplexer_1 (.in0(4'b1111), .in1(Address_M), .out(dstM), .sel(or_1_out));

  // Notes on the sheet:
  //   0xF
endmodule

module decoder_register (
  input  [63:0] ValE,
  input  [63:0] ValM,
  input  [3:0] dstE,
  input  [3:0] srcA,
  input  [3:0] dstM,
  input  [3:0] srcB,
  input  [3:0] icode,
  input  [7:0] Cycle_counter,
  input  Clk,
  output [63:0] ValA,
  output [63:0] ValB,
  output [63:0] rax,
  output [63:0] rcx,
  output [63:0] rdx,
  output [63:0] rbx,
  output [63:0] rsp,
  output [63:0] rbp,
  output [63:0] rsi,
  output [63:0] rdi,
  output [63:0] r8,
  output [63:0] r9,
  output [63:0] r10,
  output [63:0] r11,
  output [63:0] r12,
  output [63:0] r13,
  output [63:0] r14
);

  wire and_1_out, and_2_out, and_3_out, and_4_out, and_5_out, and_6_out, and_7_out, and_8_out, and_9_out,
       and_10_out, and_11_out, and_12_out, and_13_out, and_14_out, and_15_out, comparator_1_gt,
       comparator_2_eq, comparator_3_eq, decoder_1_out0, decoder_1_out1, decoder_1_out2, decoder_1_out3,
       decoder_1_out4, decoder_1_out5, decoder_1_out6, decoder_1_out7, decoder_1_out8, decoder_1_out9,
       decoder_1_out10, decoder_1_out11, decoder_1_out12, decoder_1_out13, decoder_1_out14, decoder_2_out0,
       decoder_2_out1, decoder_2_out2, decoder_2_out3, decoder_2_out4, decoder_2_out5, decoder_2_out6,
       decoder_2_out7, decoder_2_out8, decoder_2_out9, decoder_2_out10, decoder_2_out11, decoder_2_out12,
       decoder_2_out13, decoder_2_out14, decoder_3_out0, decoder_3_out1, decoder_3_out2, decoder_3_out3,
       decoder_3_out4, decoder_3_out5, decoder_3_out6, decoder_3_out7, decoder_3_out8, decoder_3_out9,
       decoder_3_out10, decoder_3_out11, decoder_3_out12, decoder_3_out13, decoder_3_out14, decoder_4_out0,
       decoder_4_out1, decoder_4_out2, decoder_4_out3, decoder_4_out4, decoder_4_out5, decoder_4_out6,
       decoder_4_out7, decoder_4_out8, decoder_4_out9, decoder_4_out10, decoder_4_out11, decoder_4_out12,
       decoder_4_out13, decoder_4_out14, or_1_out, or_2_out, or_3_out, or_4_out, or_5_out, or_6_out,
       or_7_out, or_8_out, or_9_out, or_10_out, or_11_out, or_12_out, or_13_out, or_14_out, or_15_out,
       or_16_out;
  wire [7:0] bit_extender_1_out;
  wire [63:0] controlled_buffer_1_out, controlled_buffer_2_out, controlled_buffer_4_out,
       controlled_buffer_6_out, controlled_buffer_8_out, controlled_buffer_10_out, controlled_buffer_12_out,
       controlled_buffer_14_out, controlled_buffer_16_out, controlled_buffer_18_out,
       controlled_buffer_20_out, controlled_buffer_22_out, controlled_buffer_24_out,
       controlled_buffer_26_out, controlled_buffer_28_out, multiplexer_1_out, update_rsp_1_updated;

  assign bit_extender_1_out = {{4{dstE[3]}}, dstE};  // Bit_Extender bit_extender_1
  Decoder #(.select(4)) decoder_1 (
    .out0(decoder_1_out0), .out1(decoder_1_out1), .out2(decoder_1_out2), .out3(decoder_1_out3),
    .out4(decoder_1_out4), .out5(decoder_1_out5), .out6(decoder_1_out6), .out7(decoder_1_out7),
    .out8(decoder_1_out8), .out9(decoder_1_out9), .out10(decoder_1_out10), .out11(decoder_1_out11),
    .out12(decoder_1_out12), .out13(decoder_1_out13), .out14(decoder_1_out14), .sel(dstE));  // open: out15, en
  Decoder #(.select(4)) decoder_2 (
    .out0(decoder_2_out0), .out1(decoder_2_out1), .out2(decoder_2_out2), .out3(decoder_2_out3),
    .out4(decoder_2_out4), .out5(decoder_2_out5), .out6(decoder_2_out6), .out7(decoder_2_out7),
    .out8(decoder_2_out8), .out9(decoder_2_out9), .out10(decoder_2_out10), .out11(decoder_2_out11),
    .out12(decoder_2_out12), .out13(decoder_2_out13), .out14(decoder_2_out14), .sel(dstM));  // open: out15, en
  Comparator comparator_1 (.a(Cycle_counter), .b(8'h13), .gt(comparator_1_gt));  // open: eq, lt
  assign controlled_buffer_1_out = decoder_1_out2 ? ValE : 64'bz;  // Controlled_Buffer controlled_buffer_1
  assign controlled_buffer_2_out = decoder_1_out3 ? ValE : 64'bz;  // Controlled_Buffer controlled_buffer_2
  assign controlled_buffer_2_out = decoder_2_out3 ? ValM : 64'bz;  // Controlled_Buffer controlled_buffer_3
  assign controlled_buffer_4_out = decoder_1_out4 ? ValE : 64'bz;  // Controlled_Buffer controlled_buffer_4
  assign controlled_buffer_4_out = decoder_2_out4 ? ValM : 64'bz;  // Controlled_Buffer controlled_buffer_5
  assign controlled_buffer_6_out = decoder_1_out5 ? ValE : 64'bz;  // Controlled_Buffer controlled_buffer_6
  assign controlled_buffer_6_out = decoder_2_out5 ? ValM : 64'bz;  // Controlled_Buffer controlled_buffer_7
  assign controlled_buffer_8_out = decoder_1_out6 ? ValE : 64'bz;  // Controlled_Buffer controlled_buffer_8
  assign controlled_buffer_8_out = decoder_2_out6 ? ValM : 64'bz;  // Controlled_Buffer controlled_buffer_9
  assign controlled_buffer_10_out = decoder_1_out7 ? ValE : 64'bz;  // Controlled_Buffer controlled_buffer_10
  assign controlled_buffer_10_out = decoder_2_out7 ? ValM : 64'bz;  // Controlled_Buffer controlled_buffer_11
  assign controlled_buffer_12_out = decoder_1_out8 ? ValE : 64'bz;  // Controlled_Buffer controlled_buffer_12
  assign controlled_buffer_12_out = decoder_2_out8 ? ValM : 64'bz;  // Controlled_Buffer controlled_buffer_13
  assign controlled_buffer_14_out = decoder_1_out9 ? ValE : 64'bz;  // Controlled_Buffer controlled_buffer_14
  assign controlled_buffer_14_out = decoder_2_out9 ? ValM : 64'bz;  // Controlled_Buffer controlled_buffer_15
  assign controlled_buffer_16_out = decoder_1_out10 ? ValE : 64'bz;  // Controlled_Buffer controlled_buffer_16
  assign controlled_buffer_16_out = decoder_2_out10 ? ValM : 64'bz;  // Controlled_Buffer controlled_buffer_17
  assign controlled_buffer_18_out = decoder_1_out11 ? ValE : 64'bz;  // Controlled_Buffer controlled_buffer_18
  assign controlled_buffer_18_out = decoder_2_out11 ? ValM : 64'bz;  // Controlled_Buffer controlled_buffer_19
  assign controlled_buffer_20_out = decoder_1_out12 ? ValE : 64'bz;  // Controlled_Buffer controlled_buffer_20
  assign controlled_buffer_20_out = decoder_2_out12 ? ValM : 64'bz;  // Controlled_Buffer controlled_buffer_21
  assign controlled_buffer_22_out = decoder_1_out13 ? ValE : 64'bz;  // Controlled_Buffer controlled_buffer_22
  assign controlled_buffer_22_out = decoder_2_out13 ? ValM : 64'bz;  // Controlled_Buffer controlled_buffer_23
  assign controlled_buffer_24_out = decoder_1_out14 ? ValE : 64'bz;  // Controlled_Buffer controlled_buffer_24
  assign controlled_buffer_24_out = decoder_2_out14 ? ValM : 64'bz;  // Controlled_Buffer controlled_buffer_25
  assign controlled_buffer_26_out = decoder_1_out0 ? ValE : 64'bz;  // Controlled_Buffer controlled_buffer_26
  assign controlled_buffer_26_out = decoder_2_out0 ? ValM : 64'bz;  // Controlled_Buffer controlled_buffer_27
  assign controlled_buffer_28_out = decoder_1_out1 ? ValE : 64'bz;  // Controlled_Buffer controlled_buffer_28
  assign controlled_buffer_28_out = decoder_2_out1 ? ValM : 64'bz;  // Controlled_Buffer controlled_buffer_29
  assign controlled_buffer_1_out = decoder_2_out2 ? ValM : 64'bz;  // Controlled_Buffer controlled_buffer_30
  Comparator #(.mode("unsigned"), .width(4)) comparator_2 (
    .a(icode), .b(4'b1010), .eq(comparator_2_eq));  // open: gt, lt
  Comparator #(.mode("unsigned"), .width(4)) comparator_3 (
    .a(icode), .b(4'b1011), .eq(comparator_3_eq));  // open: gt, lt
  or or_1 (or_1_out, comparator_3_eq, comparator_2_eq);
  or or_2 (or_2_out, decoder_1_out0, decoder_2_out0);
  or or_3 (or_3_out, decoder_1_out1, decoder_2_out1);
  or or_4 (or_4_out, decoder_1_out2, decoder_2_out2);
  or or_5 (or_5_out, decoder_1_out3, decoder_2_out3);
  or or_6 (or_6_out, comparator_3_eq, decoder_1_out4, decoder_2_out4, comparator_2_eq);
  or or_7 (or_7_out, decoder_1_out5, decoder_2_out5);
  or or_8 (or_8_out, decoder_1_out6, decoder_2_out6);
  or or_9 (or_9_out, decoder_1_out7, decoder_2_out7);
  or or_10 (or_10_out, decoder_1_out8, decoder_2_out8);
  or or_11 (or_11_out, decoder_1_out9, decoder_2_out9);
  or or_12 (or_12_out, decoder_1_out10, decoder_2_out10);
  or or_13 (or_13_out, decoder_1_out11, decoder_2_out11);
  or or_14 (or_14_out, decoder_1_out12, decoder_2_out12);
  or or_15 (or_15_out, decoder_1_out13, decoder_2_out13);
  or or_16 (or_16_out, decoder_1_out14, decoder_2_out14);
  and and_1 (and_1_out, comparator_1_gt, or_3_out);
  and and_2 (and_2_out, comparator_1_gt, or_4_out);
  and and_3 (and_3_out, comparator_1_gt, or_5_out);
  and and_4 (and_4_out, comparator_1_gt, or_6_out);
  and and_5 (and_5_out, comparator_1_gt, or_7_out);
  and and_6 (and_6_out, comparator_1_gt, or_8_out);
  and and_7 (and_7_out, comparator_1_gt, or_9_out);
  and and_8 (and_8_out, comparator_1_gt, or_10_out);
  and and_9 (and_9_out, comparator_1_gt, or_11_out);
  and and_10 (and_10_out, comparator_1_gt, or_12_out);
  and and_11 (and_11_out, comparator_1_gt, or_13_out);
  and and_12 (and_12_out, comparator_1_gt, or_14_out);
  and and_13 (and_13_out, comparator_1_gt, or_15_out);
  and and_14 (and_14_out, comparator_1_gt, or_16_out);
  and and_15 (and_15_out, comparator_1_gt, or_2_out);
  Register #(.width(64)) register_1 (.D(multiplexer_1_out), .en(and_4_out), .clk(Clk), .Q(rsp));  // open: clr
  Multiplexer #(.width(64)) multiplexer_1 (
    .in0(controlled_buffer_4_out), .in1(update_rsp_1_updated), .out(multiplexer_1_out), .sel(or_1_out));
  Register #(.width(64)) register_2 (.D(controlled_buffer_26_out), .en(and_15_out), .clk(Clk), .Q(rax));  // open: clr
  Register #(.width(64)) register_3 (.D(controlled_buffer_28_out), .en(and_1_out), .clk(Clk), .Q(rcx));  // open: clr
  Register #(.width(64)) register_4 (.D(controlled_buffer_1_out), .en(and_2_out), .clk(Clk), .Q(rdx));  // open: clr
  Register #(.width(64)) register_5 (.D(controlled_buffer_2_out), .en(and_3_out), .clk(Clk), .Q(rbx));  // open: clr
  Register #(.width(64)) register_6 (.D(controlled_buffer_6_out), .en(and_5_out), .clk(Clk), .Q(rbp));  // open: clr
  Register #(.width(64)) register_7 (.D(controlled_buffer_8_out), .en(and_6_out), .clk(Clk), .Q(rsi));  // open: clr
  Register #(.width(64)) register_8 (.D(controlled_buffer_10_out), .en(and_7_out), .clk(Clk), .Q(rdi));  // open: clr
  Register #(.width(64)) register_9 (.D(controlled_buffer_12_out), .en(and_8_out), .clk(Clk), .Q(r8));  // open: clr
  Register #(.width(64)) register_10 (.D(controlled_buffer_14_out), .en(and_9_out), .clk(Clk), .Q(r9));  // open: clr
  Register #(.width(64)) register_11 (.D(controlled_buffer_16_out), .en(and_10_out), .clk(Clk), .Q(r10));  // open: clr
  Register #(.width(64)) register_12 (.D(controlled_buffer_18_out), .en(and_11_out), .clk(Clk), .Q(r11));  // open: clr
  Register #(.width(64)) register_13 (.D(controlled_buffer_20_out), .en(and_12_out), .clk(Clk), .Q(r12));  // open: clr
  Register #(.width(64)) register_14 (.D(controlled_buffer_22_out), .en(and_13_out), .clk(Clk), .Q(r13));  // open: clr
  Register #(.width(64)) register_15 (.D(controlled_buffer_24_out), .en(and_14_out), .clk(Clk), .Q(r14));  // open: clr
  update_rsp update_rsp_1 (.icode(icode), .data(rsp), .updated(update_rsp_1_updated));
  assign ValA = decoder_3_out0 ? rax : 64'bz;  // Controlled_Buffer controlled_buffer_31
  assign ValB = decoder_4_out0 ? rax : 64'bz;  // Controlled_Buffer controlled_buffer_32
  assign ValB = decoder_4_out1 ? rcx : 64'bz;  // Controlled_Buffer controlled_buffer_33
  assign ValA = decoder_3_out2 ? rdx : 64'bz;  // Controlled_Buffer controlled_buffer_34
  assign ValA = decoder_3_out3 ? rbx : 64'bz;  // Controlled_Buffer controlled_buffer_35
  assign ValB = decoder_4_out3 ? rbx : 64'bz;  // Controlled_Buffer controlled_buffer_36
  assign ValA = decoder_3_out4 ? rsp : 64'bz;  // Controlled_Buffer controlled_buffer_37
  assign ValB = decoder_4_out4 ? rsp : 64'bz;  // Controlled_Buffer controlled_buffer_38
  assign ValA = decoder_3_out5 ? rbp : 64'bz;  // Controlled_Buffer controlled_buffer_39
  assign ValB = decoder_4_out5 ? rbp : 64'bz;  // Controlled_Buffer controlled_buffer_40
  assign ValA = decoder_3_out6 ? rsi : 64'bz;  // Controlled_Buffer controlled_buffer_41
  assign ValB = decoder_4_out6 ? rsi : 64'bz;  // Controlled_Buffer controlled_buffer_42
  assign ValA = decoder_3_out7 ? rdi : 64'bz;  // Controlled_Buffer controlled_buffer_43
  assign ValB = decoder_4_out7 ? rdi : 64'bz;  // Controlled_Buffer controlled_buffer_44
  assign ValA = decoder_3_out8 ? r8 : 64'bz;  // Controlled_Buffer controlled_buffer_45
  assign ValB = decoder_4_out8 ? r8 : 64'bz;  // Controlled_Buffer controlled_buffer_46
  assign ValA = decoder_3_out9 ? r9 : 64'bz;  // Controlled_Buffer controlled_buffer_47
  assign ValB = decoder_4_out9 ? r9 : 64'bz;  // Controlled_Buffer controlled_buffer_48
  assign ValA = decoder_3_out10 ? r10 : 64'bz;  // Controlled_Buffer controlled_buffer_49
  assign ValB = decoder_4_out10 ? r10 : 64'bz;  // Controlled_Buffer controlled_buffer_50
  assign ValA = decoder_3_out11 ? r11 : 64'bz;  // Controlled_Buffer controlled_buffer_51
  assign ValB = decoder_4_out11 ? r11 : 64'bz;  // Controlled_Buffer controlled_buffer_52
  assign ValA = decoder_3_out12 ? r12 : 64'bz;  // Controlled_Buffer controlled_buffer_53
  assign ValB = decoder_4_out12 ? r12 : 64'bz;  // Controlled_Buffer controlled_buffer_54
  assign ValA = decoder_3_out13 ? r13 : 64'bz;  // Controlled_Buffer controlled_buffer_55
  assign ValB = decoder_4_out13 ? r13 : 64'bz;  // Controlled_Buffer controlled_buffer_56
  assign ValA = decoder_3_out1 ? rcx : 64'bz;  // Controlled_Buffer controlled_buffer_57
  assign ValB = decoder_4_out2 ? rdx : 64'bz;  // Controlled_Buffer controlled_buffer_58
  assign ValA = decoder_3_out14 ? r14 : 64'bz;  // Controlled_Buffer controlled_buffer_59
  assign ValB = decoder_4_out14 ? r14 : 64'bz;  // Controlled_Buffer controlled_buffer_60
  Decoder #(.select(4)) decoder_3 (
    .out0(decoder_3_out0), .out1(decoder_3_out1), .out2(decoder_3_out2), .out3(decoder_3_out3),
    .out4(decoder_3_out4), .out5(decoder_3_out5), .out6(decoder_3_out6), .out7(decoder_3_out7),
    .out8(decoder_3_out8), .out9(decoder_3_out9), .out10(decoder_3_out10), .out11(decoder_3_out11),
    .out12(decoder_3_out12), .out13(decoder_3_out13), .out14(decoder_3_out14), .sel(srcA));  // open: out15, en
  Decoder #(.select(4)) decoder_4 (
    .out0(decoder_4_out0), .out1(decoder_4_out1), .out2(decoder_4_out2), .out3(decoder_4_out3),
    .out4(decoder_4_out4), .out5(decoder_4_out5), .out6(decoder_4_out6), .out7(decoder_4_out7),
    .out8(decoder_4_out8), .out9(decoder_4_out9), .out10(decoder_4_out10), .out11(decoder_4_out11),
    .out12(decoder_4_out12), .out13(decoder_4_out13), .out14(decoder_4_out14), .sel(srcB));  // open: out15, en

  // Notes on the sheet:
  //   Combinational logic to ensure that cycle count is correct, send out a 1 bit bool value.
  //   iF Cycle count is between the right values for read or write, enable the register
endmodule

module New_PC (
  input  [7:0] cycle,
  input  cnd,
  input  [3:0] icode,
  input  [63:0] ValC,
  input  [63:0] ValM,
  input  [63:0] ValP,
  input  clk,
  output [63:0] pc_new
);

  wire comparator_1_eq, comparator_2_eq, comparator_3_eq, shift_register_1_p7;
  wire [63:0] controlled_buffer_1_out, multiplexer_1_out, multiplexer_2_out;

  Comparator #(.mode("unsigned")) comparator_1 (.a(8'ha), .b(cycle), .eq(comparator_1_eq));  // open: gt, lt
  Comparator #(.mode("unsigned")) comparator_2 (.a(8'h14), .b(cycle), .eq(comparator_2_eq));  // open: gt, lt
  // Shift_Register #(.length(2)) shift_register_1: pin names not known; wires that end beside it: cnd, 1'b1, comparator_1_eq, cnd, cnd, 1'b0, shift_register_1_p7
  Multiplexer #(.width(64)) multiplexer_1 (.in0(ValP), .in1(ValC), .out(multiplexer_1_out), .sel(shift_register_1_p7));
  Comparator #(.mode("unsigned"), .width(4)) comparator_3 (
    .a(4'b0111), .b(icode), .eq(comparator_3_eq));  // open: gt, lt
  Multiplexer #(.select(4), .width(64)) multiplexer_2 (
    .in2(ValP), .in3(ValP), .in4(ValP), .in5(ValP), .in6(ValP), .in7(multiplexer_1_out), .in8(ValC),
    .in9(ValM), .in10(ValP), .in11(ValP), .out(multiplexer_2_out), .sel(icode));  // open: in0, in1, in12, in13, in14, in15
  Register #(.width(64)) register_1 (
    .D(controlled_buffer_1_out), .en(comparator_2_eq), .clk(clk), .Q(pc_new));  // open: clr
  assign controlled_buffer_1_out = comparator_2_eq ? multiplexer_2_out : 64'bz;  // Controlled_Buffer controlled_buffer_1
endmodule

module ALU (
  input  [63:0] op1,
  input  [63:0] op2,
  input  [1:0] funcType,
  output z,
  output o,
  output s,
  output [63:0] valE
);

  wire and_2_out, comparator_1_lt, comparator_2_lt, comparator_3_lt, xor_2_out;
  wire [63:0] adder_1_out, and_1_out, subtractor_1_out, xor_1_out;

  Subtractor #(.width(64)) subtractor_1 (.a(op2), .b(op1), .out(subtractor_1_out));  // open: bin, bout
  Adder #(.width(64)) adder_1 (.a(op1), .b(op2), .out(adder_1_out));  // open: cin, cout
  assign and_1_out = op1 & op2;  // AND_Gate and_1, 64 bits wide
  assign xor_1_out = op1 ^ op2;  // XOR_Gate xor_1, 64 bits wide
  Multiplexer #(.select(2), .width(64)) multiplexer_1 (
    .in0(adder_1_out), .in1(subtractor_1_out), .in2(and_1_out), .in3(xor_1_out), .out(valE), .sel(funcType));
  Comparator #(.width(64)) comparator_1 (.a(op1), .b({64{1'b0}}), .lt(comparator_1_lt));  // open: gt, eq
  Comparator #(.width(64)) comparator_2 (.a(op2), .b({64{1'b0}}), .lt(comparator_2_lt));  // open: gt, eq
  Comparator #(.width(64)) comparator_3 (.a(valE), .b({64{1'b0}}), .eq(z), .lt(comparator_3_lt));  // open: gt
  Comparator #(.width(64)) comparator_4 (.a(valE), .b({64{1'b0}}), .lt(o));  // open: gt, eq
  and and_2 (and_2_out, comparator_1_lt, comparator_2_lt);
  xor xor_2 (xor_2_out, comparator_3_lt, comparator_1_lt);
  and and_3 (s, xor_2_out, and_2_out);

  // Notes on the sheet:
  //   add
  //   sub
  //   and
  //   xor
endmodule

module ALUB (
  input  [3:0] icode,
  input  [63:0] valB,
  output [63:0] op2
);

  wire comparator_1_eq, comparator_2_eq, comparator_3_eq, comparator_4_eq, comparator_5_eq, or_1_out,
       or_2_out;

  Comparator #(.mode("unsigned"), .width(4)) comparator_1 (
    .a(icode), .b(4'b0110), .eq(comparator_1_eq));  // open: gt, lt
  Comparator #(.mode("unsigned"), .width(4)) comparator_2 (
    .a(icode), .b(4'b0100), .eq(comparator_2_eq));  // open: gt, lt
  Comparator #(.mode("unsigned"), .width(4)) comparator_3 (
    .a(icode), .b(4'b0101), .eq(comparator_3_eq));  // open: gt, lt
  Comparator #(.mode("unsigned"), .width(4)) comparator_4 (
    .a(icode), .b(4'b0011), .eq(comparator_4_eq));  // open: gt, lt
  Comparator #(.mode("unsigned"), .width(4)) comparator_5 (
    .a(icode), .b(4'b0010), .eq(comparator_5_eq));  // open: gt, lt
  or or_1 (or_1_out, comparator_1_eq, comparator_2_eq, comparator_3_eq);
  or or_2 (or_2_out, comparator_4_eq, comparator_5_eq);
  assign op2 = or_1_out ? valB : 64'bz;  // Controlled_Buffer controlled_buffer_1
  assign op2 = or_2_out ? {64{1'b0}} : 64'bz;  // Controlled_Buffer controlled_buffer_2

  // Notes on the sheet:
  //   opq
  //   rmmovq
  //   mrmovq
  //   irmovq
  //   rrmovq
endmodule

module ALUA (
  input  [3:0] icode,
  input  [63:0] val_c,
  input  [63:0] val_a,
  output [63:0] op1
);

  wire comparator_1_eq, comparator_2_eq, comparator_3_eq, comparator_4_eq, comparator_5_eq, or_1_out,
       or_2_out;

  Comparator #(.mode("unsigned"), .width(4)) comparator_1 (
    .a(icode), .b(4'b0010), .eq(comparator_1_eq));  // open: gt, lt
  Comparator #(.mode("unsigned"), .width(4)) comparator_2 (
    .a(icode), .b(4'b0110), .eq(comparator_2_eq));  // open: gt, lt
  Comparator #(.mode("unsigned"), .width(4)) comparator_3 (
    .a(icode), .b(4'b0011), .eq(comparator_3_eq));  // open: gt, lt
  Comparator #(.mode("unsigned"), .width(4)) comparator_4 (
    .a(icode), .b(4'b0100), .eq(comparator_4_eq));  // open: gt, lt
  Comparator #(.mode("unsigned"), .width(4)) comparator_5 (
    .a(icode), .b(4'b0101), .eq(comparator_5_eq));  // open: gt, lt
  or or_1 (or_1_out, comparator_3_eq, comparator_4_eq, comparator_5_eq);
  or or_2 (or_2_out, comparator_1_eq, comparator_2_eq);
  assign op1 = or_1_out ? val_c : 64'bz;  // Controlled_Buffer controlled_buffer_1
  assign op1 = or_2_out ? val_a : 64'bz;  // Controlled_Buffer controlled_buffer_2

  // Notes on the sheet:
  //   rrmovq
  //   opq
  //   rmmovq
  //   mrmovq
  //   irmovq
endmodule

module setCC (
  input  [3:0] icode,
  output set_cc
);

  wire comparator_1_eq;

  Comparator #(.mode("unsigned"), .width(4)) comparator_1 (
    .a(icode), .b(4'b0110), .eq(comparator_1_eq));  // open: gt, lt
  Multiplexer multiplexer_1 (.in0(1'b0), .in1(1'b1), .out(set_cc), .sel(comparator_1_eq));
endmodule

module cond_exec (
  input  [7:0] cycles,
  input  clk,
  input  [3:0] ifun,
  input  setcc,
  input  z,
  input  s,
  input  o,
  output cond
);

  wire and_1_out, and_2_out, comparator_1_eq, multiplexer_1_out, not_1_out, not_2_out, not_3_out, not_4_out,
       or_1_out, xor_1_out;

  not not_1 (not_1_out, z);
  not not_2 (not_2_out, s);
  not not_3 (not_3_out, o);
  Comparator #(.mode("unsigned")) comparator_1 (.a(cycles), .b(8'ha), .eq(comparator_1_eq));  // open: gt, lt
  and and_1 (and_1_out, comparator_1_eq, clk, setcc);
  xor xor_1 (xor_1_out, s, o);
  or or_1 (or_1_out, xor_1_out, z);
  not not_4 (not_4_out, xor_1_out);
  and and_2 (and_2_out, not_4_out, not_1_out);
  Multiplexer #(.select(4)) multiplexer_1 (
    .in0(1'b1), .in1(or_1_out), .in2(xor_1_out), .in3(z), .in4(not_1_out), .in5(not_4_out), .in6(and_2_out),
    .out(multiplexer_1_out), .sel(ifun));  // open: in7, in8, in9, in10, in11, in12, in13, in14, in15
  D_Flip_Flop d_ff_1 (.D(multiplexer_1_out), .clk(and_1_out), .Q(cond));  // open: Qn, preset, reset
endmodule

module execute (
  input  [7:0] cyc_cnt,
  input  clk,
  input  [3:0] icode,
  input  [3:0] ifun,
  input  [63:0] valC,
  input  [63:0] valA,
  input  [63:0] valB,
  output condition,
  output [63:0] valE
);

  wire alu_1_o, alu_1_s, alu_1_z, setcc_1_set_cc;
  wire [1:0] alufun_1_out_3;
  wire [63:0] alua_1_op1, alub_1_op2;

  setCC setcc_1 (.icode(icode), .set_cc(setcc_1_set_cc));
  ALUA alua_1 (.icode(icode), .val_c(valC), .val_a(valA), .op1(alua_1_op1));
  ALUB alub_1 (.icode(icode), .valB(valB), .op2(alub_1_op2));
  ALUFUN alufun_1 (.ifun(ifun), .icode(icode), .out_3(alufun_1_out_3));
  ALU alu_1 (
    .op1(alua_1_op1), .op2(alub_1_op2), .funcType(alufun_1_out_3), .z(alu_1_z), .o(alu_1_o), .s(alu_1_s),
    .valE(valE));
  cond_exec cond_exec_1 (
    .cycles(cyc_cnt), .clk(clk), .ifun(ifun), .setcc(setcc_1_set_cc), .z(alu_1_z), .s(alu_1_s), .o(alu_1_o),
    .cond(condition));
endmodule

module ALUFUN (
  input  [3:0] ifun,
  input  [3:0] icode,
  output [1:0] out_3
);

  wire comparator_1_eq, comparator_2_eq, or_1_out;
  wire [3:2] multiplexer_1_out;

  Comparator #(.mode("unsigned"), .width(4)) comparator_1 (
    .a(4'b0111), .b(icode), .eq(comparator_1_eq));  // open: gt, lt
  Comparator #(.mode("unsigned"), .width(4)) comparator_2 (
    .a(icode), .b(4'b0110), .eq(comparator_2_eq));  // open: gt, lt
  or or_1 (or_1_out, comparator_1_eq, comparator_2_eq);
  Multiplexer #(.width(4)) multiplexer_1 (.in0(4'b0000), .in1(ifun), .out({multiplexer_1_out, out_3}), .sel(or_1_out));
endmodule

module memRead (
  input  [3:0] icode,
  output read
);

  wire comparator_1_eq, comparator_2_eq, comparator_3_eq;

  Comparator #(.mode("unsigned"), .width(4)) comparator_1 (
    .a(icode), .b(4'b0101), .eq(comparator_1_eq));  // open: gt, lt
  Comparator #(.mode("unsigned"), .width(4)) comparator_2 (
    .a(icode), .b(4'b1001), .eq(comparator_2_eq));  // open: gt, lt
  Comparator #(.mode("unsigned"), .width(4)) comparator_3 (
    .a(icode), .b(4'b1011), .eq(comparator_3_eq));  // open: gt, lt
  or or_1 (read, comparator_1_eq, comparator_2_eq, comparator_3_eq);
endmodule

module memWrite (
  input  [3:0] icode,
  output write
);

  wire comparator_1_eq, comparator_2_eq, comparator_3_eq, comparator_4_eq;

  Comparator #(.mode("unsigned"), .width(4)) comparator_1 (
    .a(icode), .b(4'b0010), .eq(comparator_1_eq));  // open: gt, lt
  Comparator #(.mode("unsigned"), .width(4)) comparator_2 (
    .a(icode), .b(4'b0100), .eq(comparator_2_eq));  // open: gt, lt
  Comparator #(.mode("unsigned"), .width(4)) comparator_3 (
    .a(icode), .b(4'b1000), .eq(comparator_3_eq));  // open: gt, lt
  Comparator #(.mode("unsigned"), .width(4)) comparator_4 (
    .a(icode), .b(4'b1010), .eq(comparator_4_eq));  // open: gt, lt
  or or_1 (write, comparator_1_eq, comparator_2_eq, comparator_3_eq, comparator_4_eq);
endmodule

module memAddr (
  input  [63:0] ValE,
  input  [63:0] ValA,
  input  [3:0] icode,
  output [63:0] addr
);

  wire comparator_1_eq, comparator_2_eq, comparator_3_eq, comparator_4_eq, comparator_5_eq, comparator_6_eq,
       comparator_7_eq;
  wire [1:0] or_1_out;

  Comparator #(.mode("unsigned"), .width(4)) comparator_1 (
    .a(icode), .b(4'b0010), .eq(comparator_1_eq));  // open: gt, lt
  Comparator #(.mode("unsigned"), .width(4)) comparator_2 (
    .a(icode), .b(4'b0100), .eq(comparator_2_eq));  // open: gt, lt
  Comparator #(.mode("unsigned"), .width(4)) comparator_3 (
    .a(icode), .b(4'b0101), .eq(comparator_3_eq));  // open: gt, lt
  Comparator #(.mode("unsigned"), .width(4)) comparator_4 (
    .a(icode), .b(4'b1000), .eq(comparator_4_eq));  // open: gt, lt
  Comparator #(.mode("unsigned"), .width(4)) comparator_5 (
    .a(icode), .b(4'b1010), .eq(comparator_5_eq));  // open: gt, lt
  Comparator #(.mode("unsigned"), .width(4)) comparator_6 (
    .a(icode), .b(4'b1001), .eq(comparator_6_eq));  // open: gt, lt
  Comparator #(.mode("unsigned"), .width(4)) comparator_7 (
    .a(icode), .b(4'b1011), .eq(comparator_7_eq));  // open: gt, lt
  or or_1 (or_1_out[0], comparator_1_eq, comparator_2_eq, comparator_3_eq, comparator_4_eq, comparator_5_eq);
  or or_2 (or_1_out[1], comparator_6_eq, comparator_7_eq);
  Multiplexer #(.select(2), .width(64)) multiplexer_1 (
    .in1(ValE), .in2(ValA), .out(addr), .sel(or_1_out));  // open: in0, in3
endmodule

module memData (
  input  [63:0] ValP,
  input  [63:0] ValA,
  input  [3:0] icode,
  output [63:0] data
);

  wire comparator_1_eq, comparator_2_eq, comparator_3_eq;
  wire [1:0] or_1_out;

  Comparator #(.mode("unsigned"), .width(4)) comparator_1 (
    .a(icode), .b(4'b0010), .eq(comparator_1_eq));  // open: gt, lt
  Comparator #(.mode("unsigned"), .width(4)) comparator_2 (
    .a(icode), .b(4'b0100), .eq(comparator_2_eq));  // open: gt, lt
  Comparator #(.mode("unsigned"), .width(4)) comparator_3 (
    .a(icode), .b(4'b1010), .eq(comparator_3_eq));  // open: gt, lt
  Comparator #(.mode("unsigned"), .width(4)) comparator_4 (.a(icode), .b(4'b1000), .eq(or_1_out[1]));  // open: gt, lt
  or or_1 (or_1_out[0], comparator_1_eq, comparator_2_eq, comparator_3_eq);
  Multiplexer #(.select(2), .width(64)) multiplexer_1 (
    .in1(ValA), .in2(ValP), .out(data), .sel(or_1_out));  // open: in0, in3
endmodule

module mainMem (
  input  [3:0] icode,
  input  [63:0] ValE,
  input  [63:0] ValA,
  input  [63:0] ValP,
  input  Clk,
  input  [7:0] cycle_count,
  output [63:0] ValM
);

  wire and_1_out, comparator_1_gt, comparator_2_gt, comparator_3_eq, decoder_1_out0, decoder_1_out1,
       decoder_1_out2, decoder_1_out3, decoder_1_out4, decoder_1_out5, decoder_1_out6, decoder_1_out7,
       memread_1_read, memwrite_1_write, multiplexer_1_out;
  wire [7:0] adder_1_out, demultiplexer_1_out0, demultiplexer_1_out1, demultiplexer_1_out2,
       demultiplexer_1_out3, demultiplexer_1_out4, demultiplexer_1_out5, demultiplexer_1_out6,
       demultiplexer_1_out7, multiplexer_2_out, multiplexer_3_out, ram_1_dout, register_1_q;
  wire [11:0] adder_2_out, bit_extender_1_out;
  wire [63:0] memaddr_1_addr, memdata_1_data;

  Register register_1 (.D(multiplexer_2_out), .clk(multiplexer_1_out), .Q(register_1_q));  // open: en, clr
  Comparator #(.mode("unsigned")) comparator_1 (.a(cycle_count), .b(8'ha), .gt(comparator_1_gt));  // open: eq, lt
  Comparator #(.mode("unsigned")) comparator_2 (.a(8'h13), .b(cycle_count), .gt(comparator_2_gt));  // open: eq, lt
  Adder adder_1 (.a(register_1_q), .b(8'h1), .out(adder_1_out));  // open: cin, cout
  Multiplexer multiplexer_1 (.in0(1'b0), .in1(Clk), .out(multiplexer_1_out), .sel(and_1_out));
  and and_1 (and_1_out, comparator_1_gt, comparator_2_gt);
  Comparator #(.mode("unsigned")) comparator_3 (.a(adder_1_out), .b(8'h8), .eq(comparator_3_eq));  // open: gt, lt
  memAddr memaddr_1 (.ValE(ValE), .ValA(ValA), .icode(icode), .addr(memaddr_1_addr));
  memWrite memwrite_1 (.icode(icode), .write(memwrite_1_write));
  memRead memread_1 (.icode(icode), .read(memread_1_read));
  memData memdata_1 (.ValP(ValP), .ValA(ValA), .icode(icode), .data(memdata_1_data));
  Multiplexer #(.width(8)) multiplexer_2 (
    .in0(adder_1_out), .in1({8{1'b0}}), .out(multiplexer_2_out), .sel(comparator_3_eq));
  assign bit_extender_1_out = {{4{1'b0}}, multiplexer_2_out};  // Bit_Extender bit_extender_1
  Adder #(.width(12)) adder_2 (.a(memaddr_1_addr[11:0]), .b(bit_extender_1_out), .out(adder_2_out));  // open: cin, cout
  Multiplexer #(.select(3), .width(8)) multiplexer_3 (
    .in0(memdata_1_data[7:0]), .in1(memdata_1_data[15:8]), .in2(memdata_1_data[23:16]),
    .in3(memdata_1_data[31:24]), .in4(memdata_1_data[39:32]), .in5(memdata_1_data[47:40]),
    .in6(memdata_1_data[55:48]), .in7(memdata_1_data[63:56]), .out(multiplexer_3_out),
    .sel(bit_extender_1_out[2:0]));
  RAM #(.addrWidth(12)) ram_1 (
    .addr(adder_2_out), .we(memwrite_1_write), .oe(memread_1_read), .clk(multiplexer_1_out),
    .din(multiplexer_3_out), .dout(ram_1_dout));
  Demultiplexer #(.select(3), .width(8)) demultiplexer_1 (
    .out0(demultiplexer_1_out0), .out1(demultiplexer_1_out1), .out2(demultiplexer_1_out2),
    .out3(demultiplexer_1_out3), .out4(demultiplexer_1_out4), .out5(demultiplexer_1_out5),
    .out6(demultiplexer_1_out6), .out7(demultiplexer_1_out7), .in(ram_1_dout), .sel(bit_extender_1_out[2:0]));
  Decoder #(.enable("false"), .select(3)) decoder_1 (
    .out0(decoder_1_out0), .out1(decoder_1_out1), .out2(decoder_1_out2), .out3(decoder_1_out3),
    .out4(decoder_1_out4), .out5(decoder_1_out5), .out6(decoder_1_out6), .out7(decoder_1_out7),
    .sel(bit_extender_1_out[2:0]));
  Register register_2 (
    .D(demultiplexer_1_out0), .en(decoder_1_out0), .clk(multiplexer_1_out), .Q(ValM[63:56]));  // open: clr
  Register register_3 (
    .D(demultiplexer_1_out1), .en(decoder_1_out1), .clk(multiplexer_1_out), .Q(ValM[7:0]));  // open: clr
  Register register_4 (
    .D(demultiplexer_1_out2), .en(decoder_1_out2), .clk(multiplexer_1_out), .Q(ValM[15:8]));  // open: clr
  Register register_5 (
    .D(demultiplexer_1_out3), .en(decoder_1_out3), .clk(multiplexer_1_out), .Q(ValM[23:16]));  // open: clr
  Register register_6 (
    .D(demultiplexer_1_out4), .en(decoder_1_out4), .clk(multiplexer_1_out), .Q(ValM[31:24]));  // open: clr
  Register register_7 (
    .D(demultiplexer_1_out5), .en(decoder_1_out5), .clk(multiplexer_1_out), .Q(ValM[39:32]));  // open: clr
  Register register_8 (
    .D(demultiplexer_1_out6), .en(decoder_1_out6), .clk(multiplexer_1_out), .Q(ValM[47:40]));  // open: clr
  Register register_9 (
    .D(demultiplexer_1_out7), .en(decoder_1_out7), .clk(multiplexer_1_out), .Q(ValM[55:48]));  // open: clr
endmodule

module cycle_20 (
  input  Clk,
  output [7:0] Cycle_Count
);

  wire comparator_1_eq;
  wire [7:0] adder_1_out, multiplexer_1_out;

  Multiplexer #(.width(8)) multiplexer_1 (
    .in0(adder_1_out), .in1({8{1'b0}}), .out(multiplexer_1_out), .sel(comparator_1_eq));
  Register register_1 (.D(multiplexer_1_out), .clk(Clk), .Q(Cycle_Count));  // open: en, clr
  Adder adder_1 (.a(Cycle_Count), .b(8'h1), .out(adder_1_out));  // open: cin, cout
  Comparator #(.mode("unsigned")) comparator_1 (.a(adder_1_out), .b(8'h15), .eq(comparator_1_eq));  // open: gt, lt

  // Notes on the sheet:
  //   cycle count
endmodule

module update_rsp (
  input  [3:0] icode,
  input  [63:0] data,
  output [63:0] updated
);

  wire comparator_1_eq, comparator_2_eq, or_1_out;
  wire [63:0] adder_1_out, multiplexer_1_out, subtractor_1_out;

  Comparator #(.mode("unsigned"), .width(4)) comparator_1 (
    .a(4'b1010), .b(icode), .eq(comparator_1_eq));  // open: gt, lt
  Comparator #(.mode("unsigned"), .width(4)) comparator_2 (
    .a(icode), .b(4'b1011), .eq(comparator_2_eq));  // open: gt, lt
  or or_1 (or_1_out, comparator_1_eq, comparator_2_eq);
  Subtractor #(.width(64)) subtractor_1 (.a(data), .b(64'h8), .out(subtractor_1_out));  // open: bin, bout
  Adder #(.width(64)) adder_1 (.a(64'h8), .b(data), .out(adder_1_out));  // open: cin, cout
  Multiplexer #(.width(64)) multiplexer_1 (
    .in0(subtractor_1_out), .in1(adder_1_out), .out(multiplexer_1_out), .sel(comparator_2_eq));
  Multiplexer #(.width(64)) multiplexer_2 (.in0(data), .in1(multiplexer_1_out), .out(updated), .sel(or_1_out));

  // Notes on the sheet:
  //   push
  //   pop
endmodule
